// Logisim project CombinationalLogic.circ as structural Verilog: 14 circuits, main circuit main1
module main1 (
  input  in_1,
  input  in_2,
  input  in_3,
  input  in_4,
  input  in_5,
  input  in_6,
  input  [2:0] in_7,
  input  [2:0] in_8,
  input  [1:0] in_9,
  input  [2:0] in_10,
  input  [2:0] in_11,
  input  in_12,
  input  in_13,
  input  in_14,
  input  [3:0] in_15,
  input  [3:0] in_16,
  input  Bin,
  input  A,
  input  B,
  input  \_4_2编码器 ,
  input  in_21,
  input  in_22,
  input  in_23,
  input  \_4_2优先编码器 ,
  input  in_25,
  input  in_26,
  input  in_27,
  input  \_4_2优先编码器2 ,
  input  in_29,
  input  in_30,
  input  in_31,
  input  \_4_2优先编码器3 ,
  input  in_33,
  input  in_34,
  input  in_35,
  input  [3:0] in_36,
  input  [3:0] in_37,
  input  [3:0] in_38,
  input  [3:0] in_39,
  input  [3:0] in_40,
  input  [3:0] in_41,
  output out_42,
  output out_43,
  output out_44,
  output out_45,
  output out_46,
  output out_47,
  output out_48,
  output out_49,
  output [2:0] out_50,
  output out_51,
  output out_52,
  output out_53,
  output D,
  output Bout,
  output out_56,
  output out_57,
  output l,
  output h,
  output out_60,
  output out_61,
  output out_62,
  output out_63,
  output [3:0] out_64
);

  wire and_2_out, and_3_out, and_4_out, and_5_out, and_6_out, and_7_out, and_8_out, and_9_out, and_10_out,
       and_11_out, and_12_out, and_13_out, and_14_out, and_23_out, and_24_out, and_37_out, and_38_out,
       and_44_out, decoder2_4_1_out_3, decoder2_4_1_out_4, decoder2_4_1_out_5, decoder2_4_1_out_6,
       decoder2_4_2_out_3, decoder2_4_2_out_4, decoder2_4_2_out_5, decoder2_4_2_out_6, decoder2_4_3_out_3,
       decoder2_4_3_out_4, decoder2_4_3_out_5, decoder2_4_3_out_6, decoder2_4_4_out_3, decoder2_4_4_out_4,
       decoder2_4_4_out_5, decoder2_4_4_out_6, decoder2_4_5_out_3, decoder2_4_5_out_4, decoder2_4_5_out_5,
       decoder2_4_5_out_6, decoder_1_out0, decoder_1_out1, decoder_1_out2, decoder_1_out3, decoder_1_out4,
       decoder_1_out5, decoder_1_out6, decoder_1_out7, decoder_1_out8, decoder_1_out9, decoder_1_out10,
       decoder_1_out11, decoder_1_out12, decoder_1_out13, decoder_1_out14, decoder_1_out15, decoder_2_out0,
       decoder_2_out1, decoder_2_out2, decoder_2_out3, decoder_3_out0, decoder_3_out1, decoder_3_out2,
       decoder_3_out3, decoder_3_out4, decoder_3_out5, decoder_3_out6, decoder_3_out7, decoder_3_out8,
       decoder_3_out9, decoder_3_out10, decoder_3_out11, decoder_3_out12, decoder_3_out13, decoder_3_out14,
       decoder_3_out15, dipswitch_1_p1, dipswitch_1_p2, dipswitch_1_p3, dipswitch_1_p4, dipswitch_1_p5,
       dipswitch_1_p6, dipswitch_1_p7, dipswitch_1_p8, dipswitch_1_p9, dipswitch_1_p10, dipswitch_1_p11,
       dipswitch_1_p12, dipswitch_1_p13, dipswitch_1_p14, dipswitch_1_p15, dipswitch_1_p16, dipswitch_2_p1,
       dipswitch_5_p1, dipswitch_5_p2, dipswitch_5_p3, dipswitch_6_p1, dipswitch_6_p2, dipswitch_6_p3,
       dipswitch_6_p4, dipswitch_6_p5, dipswitch_7_p1, dipswitch_7_p2, dipswitch_7_p3, dipswitch_7_p4,
       dipswitch_8_p1, dipswitch_8_p2, dipswitch_8_p3, dipswitch_8_p4, full_adder_1_cout, full_adder_2_cout,
       full_adder_3_cout, full_suber_1_bout, full_suber_2_bout, full_suber_3_bout, half_adder_1_c,
       half_adder_1_s, half_adder_2_c, half_adder_3_c, half_suber_1_bo, half_suber_1_d, half_suber_2_bo,
       half_suber_3_bo, not_1_out, not_2_out, not_3_out, not_4_out, not_5_out, not_6_out, not_7_out,
       not_8_out, not_9_out, not_10_out, not_11_out, not_12_out, not_13_out, not_14_out, not_15_out,
       not_16_out, or_1_out, or_6_out, or_7_out, or_8_out, or_9_out, or_10_out, or_11_out, or_12_out,
       or_21_out, or_23_out, or_24_out, or_27_out, or_28_out, or_29_out, or_30_out, or_31_out,
       seven_segment_circuit10_1_out_2, seven_segment_circuit10_1_out_3, seven_segment_circuit10_1_out_4,
       seven_segment_circuit10_1_out_5, seven_segment_circuit10_1_out_6, seven_segment_circuit10_1_out_7,
       seven_segment_circuit10_1_out_8, seven_segment_circuit10_1_out_9, seven_segment_circuit16_1_a,
       seven_segment_circuit16_1_b, seven_segment_circuit16_1_c, seven_segment_circuit16_1_d,
       seven_segment_circuit16_1_e, seven_segment_circuit16_1_f, seven_segment_circuit16_1_g,
       seven_segment_circuit16_2_a, seven_segment_circuit16_2_b, seven_segment_circuit16_2_c,
       seven_segment_circuit16_2_d, seven_segment_circuit16_2_e, seven_segment_circuit16_2_f,
       seven_segment_circuit16_2_g, seven_segment_circuit16_3_a, seven_segment_circuit16_3_b,
       seven_segment_circuit16_3_c, seven_segment_circuit16_3_d, seven_segment_circuit16_3_e,
       seven_segment_circuit16_3_f, seven_segment_circuit16_3_g, seven_segment_circuit16_4_a,
       seven_segment_circuit16_4_b, seven_segment_circuit16_4_c, seven_segment_circuit16_4_d,
       seven_segment_circuit16_4_e, seven_segment_circuit16_4_f, seven_segment_circuit16_4_g,
       seven_segment_circuit16_5_a, seven_segment_circuit16_5_b, seven_segment_circuit16_5_c,
       seven_segment_circuit16_5_d, seven_segment_circuit16_5_e, seven_segment_circuit16_5_f,
       seven_segment_circuit16_5_g, seven_segment_circuit16_6_a, seven_segment_circuit16_6_b,
       seven_segment_circuit16_6_c, seven_segment_circuit16_6_d, seven_segment_circuit16_6_e,
       seven_segment_circuit16_6_f, seven_segment_circuit16_6_g, seven_segment_circuit16_7_a,
       seven_segment_circuit16_7_b, seven_segment_circuit16_7_c, seven_segment_circuit16_7_d,
       seven_segment_circuit16_7_e, seven_segment_circuit16_7_f, seven_segment_circuit16_7_g,
       seven_segment_circuit16_8_a, seven_segment_circuit16_8_b, seven_segment_circuit16_8_c,
       seven_segment_circuit16_8_d, seven_segment_circuit16_8_e, seven_segment_circuit16_8_f,
       seven_segment_circuit16_8_g, seven_segment_circuit16_9_a, seven_segment_circuit16_9_b,
       seven_segment_circuit16_9_c, seven_segment_circuit16_9_d, seven_segment_circuit16_9_e,
       seven_segment_circuit16_9_f, seven_segment_circuit16_9_g, sign_magnitude_adder_4bit_1_s,
       suber_4_1_bout, suber_4_2_bout, xnor_1_out, xnor_2_out, xnor_3_out, xnor_4_out;
  wire [0:0] adder_4_2_cout;
  wire [2:0] and_25_out, and_26_out, and_27_out, and_28_out, bit_extender_1_out, bit_extender_2_out,
       bit_extender_3_out, bit_extender_4_out, not_17_out, not_23_out, not_25_out, or_35_out,
       sign_magnitude_adder_4bit_1_o0;
  wire [3:0] adder_4_1_s, adder_4_2_s, adder_4_3_s, and_29_out, and_30_out, and_31_out, and_32_out,
       and_33_out, and_34_out, and_35_out, and_36_out, and_39_out, and_40_out, and_41_out, and_42_out,
       and_43_out, bit_extender_5_out, bit_extender_6_out, bit_extender_7_out, bit_extender_8_out,
       bit_extender_9_out, bit_extender_10_out, bit_extender_11_out, bit_extender_12_out,
       bit_extender_13_out, bit_extender_14_out, dipswitch_3_p4, dipswitch_4_p4, half_adder_2_s,
       half_suber_3_d, low1_out, not_20_out, not_24_out, not_28_out, or_25_out, or_26_out, or_32_out,
       suber_4_1_d, suber_4_2_d, undriven;
  wire [3:3] or_33_out, or_35_out_2;

  // DipSwitch #(.number(16)) dipswitch_1: pin names not known; wires that end beside it: dipswitch_1_p1, dipswitch_1_p2, dipswitch_1_p3, dipswitch_1_p4, dipswitch_1_p5, dipswitch_1_p6, dipswitch_1_p7, dipswitch_1_p8, dipswitch_1_p9, dipswitch_1_p10, dipswitch_1_p11, dipswitch_1_p12, dipswitch_1_p13, dipswitch_1_p14, dipswitch_1_p15, dipswitch_1_p16
  not not_1 (not_1_out, in_1);
  not not_2 (not_2_out, in_4);
  not not_3 (not_3_out, in_6);
  Decoder #(.enable("false"), .select(4)) decoder_1 (
    .out0(decoder_1_out0), .out1(decoder_1_out1), .out2(decoder_1_out2), .out3(decoder_1_out3),
    .out4(decoder_1_out4), .out5(decoder_1_out5), .out6(decoder_1_out6), .out7(decoder_1_out7),
    .out8(decoder_1_out8), .out9(decoder_1_out9), .out10(decoder_1_out10), .out11(decoder_1_out11),
    .out12(decoder_1_out12), .out13(decoder_1_out13), .out14(decoder_1_out14), .out15(decoder_1_out15),
    .sel(in_15));
  or low1 (low1_out[0], dipswitch_1_p2, dipswitch_1_p4, dipswitch_1_p6, dipswitch_1_p8, dipswitch_1_p10, dipswitch_1_p12, dipswitch_1_p14, dipswitch_1_p16);
  or or_1 (or_1_out, decoder_1_out15, decoder_1_out14, decoder_1_out13, decoder_1_out12, decoder_1_out11, decoder_1_out10);
  or or_2 (low1_out[1], dipswitch_1_p3, dipswitch_1_p4, dipswitch_1_p7, dipswitch_1_p8, dipswitch_1_p11, dipswitch_1_p12, dipswitch_1_p15, dipswitch_1_p16);
  or or_3 (low1_out[2], dipswitch_1_p5, dipswitch_1_p6, dipswitch_1_p7, dipswitch_1_p8, dipswitch_1_p13, dipswitch_1_p14, dipswitch_1_p15, dipswitch_1_p16);
  or high1 (low1_out[3], dipswitch_1_p9, dipswitch_1_p10, dipswitch_1_p11, dipswitch_1_p12, dipswitch_1_p13, dipswitch_1_p14, dipswitch_1_p15, dipswitch_1_p16);
  or or_4 (out_56, in_21, in_23);
  or or_5 (out_57, in_22, in_23);
  decoder2_4 decoder2_4_1 (
    .in_1(in_1), .in_2(not_2_out), .out_3(decoder2_4_1_out_3), .out_4(decoder2_4_1_out_4),
    .out_5(decoder2_4_1_out_5), .out_6(decoder2_4_1_out_6));
  decoder2_4 decoder2_4_2 (
    .in_1(not_1_out), .in_2(in_4), .out_3(decoder2_4_2_out_3), .out_4(decoder2_4_2_out_4),
    .out_5(decoder2_4_2_out_5), .out_6(decoder2_4_2_out_6));
  decoder2_4 decoder2_4_3 (
    .in_1(in_4), .in_2(in_6), .out_3(decoder2_4_3_out_3), .out_4(decoder2_4_3_out_4),
    .out_5(decoder2_4_3_out_5), .out_6(decoder2_4_3_out_6));
  decoder2_4 decoder2_4_4 (
    .in_1(not_2_out), .in_2(not_3_out), .out_3(decoder2_4_4_out_3), .out_4(decoder2_4_4_out_4),
    .out_5(decoder2_4_4_out_5), .out_6(decoder2_4_4_out_6));
  _7_Segment_Display u_7_segment_display_1 (
    .g(seven_segment_circuit16_1_g), .f(seven_segment_circuit16_1_f), .a(seven_segment_circuit16_1_a),
    .b(seven_segment_circuit16_1_b), .e(seven_segment_circuit16_1_e), .d(seven_segment_circuit16_1_d),
    .c(seven_segment_circuit16_1_c));  // open: dp
  not not_4 (not_4_out, in_25);
  // AND_Gate and_1 has open pins: in0=\_4_2优先编码器 , in1=not_4_out, in2=not_5_out, in3=not_6_out, out=open
  not not_5 (not_5_out, in_26);
  not not_6 (not_6_out, in_27);
  not not_7 (not_7_out, in_26);
  and and_2 (and_2_out, in_25, not_7_out, not_8_out);
  not not_8 (not_8_out, in_27);
  and and_3 (and_3_out, in_26, not_9_out);
  not not_9 (not_9_out, in_27);
  not not_10 (not_10_out, in_30);
  and and_4 (and_4_out, in_29, not_10_out, not_11_out);
  not not_11 (not_11_out, in_31);
  and and_5 (and_5_out, in_30, not_12_out);
  not not_12 (not_12_out, in_31);
  not not_13 (not_13_out, in_34);
  and and_6 (and_6_out, in_33, not_13_out, not_14_out);
  not not_14 (not_14_out, in_35);
  and and_7 (and_7_out, decoder2_4_1_out_3, decoder2_4_2_out_6);
  and and_8 (and_8_out, decoder2_4_1_out_4, decoder2_4_2_out_5);
  and and_9 (and_9_out, decoder2_4_1_out_6, decoder2_4_2_out_3);
  and and_10 (and_10_out, decoder2_4_1_out_5, decoder2_4_2_out_4);
  and and_11 (and_11_out, decoder2_4_3_out_4, decoder2_4_4_out_5);
  and and_12 (and_12_out, decoder2_4_3_out_3, decoder2_4_4_out_6);
  and and_13 (and_13_out, decoder2_4_3_out_5, decoder2_4_4_out_4);
  and and_14 (and_14_out, decoder2_4_3_out_6, decoder2_4_4_out_3);
  seven_segment_circuit16 seven_segment_circuit16_1 (
    .in_1(low1_out), .a(seven_segment_circuit16_1_a), .b(seven_segment_circuit16_1_b),
    .c(seven_segment_circuit16_1_c), .d(seven_segment_circuit16_1_d), .e(seven_segment_circuit16_1_e),
    .f(seven_segment_circuit16_1_f), .g(seven_segment_circuit16_1_g));
  or or_6 (or_6_out, decoder_1_out0, decoder_1_out2, decoder_1_out3, decoder_1_out9, decoder_1_out5, decoder_1_out6, decoder_1_out7, decoder_1_out8);
  or or_7 (or_7_out, decoder_1_out0, decoder_1_out1, decoder_1_out2, decoder_1_out3, decoder_1_out4, decoder_1_out8, decoder_1_out7, decoder_1_out9);
  or or_8 (or_8_out, decoder_1_out0, decoder_1_out1, decoder_1_out3, decoder_1_out4, decoder_1_out5, decoder_1_out6, decoder_1_out7, decoder_1_out8, decoder_1_out9);
  or or_9 (or_9_out, decoder_1_out0, decoder_1_out2, decoder_1_out3, decoder_1_out5, decoder_1_out6, decoder_1_out8, decoder_1_out9);
  or or_10 (or_10_out, decoder_1_out0, decoder_1_out2, decoder_1_out6, decoder_1_out8);
  or or_11 (or_11_out, decoder_1_out0, decoder_1_out4, decoder_1_out5, decoder_1_out6, decoder_1_out8, decoder_1_out9);
  or or_12 (or_12_out, decoder_1_out2, decoder_1_out3, decoder_1_out4, decoder_1_out5, decoder_1_out6, decoder_1_out8, decoder_1_out9);
  or or_13 (l, in_27, and_2_out);
  or or_14 (h, and_3_out, in_27);
  or or_15 (out_60, in_31, and_4_out);
  or or_16 (out_61, and_5_out, in_31);
  or or_17 (out_62, and_6_out, in_35);
  or or_18 (out_63, in_34, in_35);
  and and_15 (out_42, and_8_out, and_12_out);
  and and_16 (out_43, and_8_out, and_11_out);
  and and_17 (out_45, and_7_out, and_13_out);
  and and_18 (out_46, and_7_out, and_14_out);
  and and_19 (out_47, and_12_out, and_9_out);
  and and_20 (out_48, and_9_out, and_11_out);
  buf and_21 (out_49, and_13_out);  // AND_Gate
  and and_22 (out_51, and_10_out, and_14_out);
  _7_Segment_Display u_7_segment_display_2 (
    .g(or_12_out), .f(or_11_out), .a(or_6_out), .b(or_7_out), .e(or_10_out), .d(or_9_out), .c(or_8_out),
    .dp(or_1_out));
  Decoder #(.enable("false"), .select(2)) decoder_2 (
    .out0(decoder_2_out0), .out1(decoder_2_out1), .out2(decoder_2_out2), .out3(decoder_2_out3), .sel(in_9));
  not not_15 (not_15_out, in_3);
  assign bit_extender_1_out = {{2{decoder_2_out0}}, decoder_2_out0};  // Bit_Extender bit_extender_1
  and and_23 (and_23_out, in_2, not_15_out);
  and and_24 (and_24_out, in_3, in_5);
  assign bit_extender_2_out = {{2{decoder_2_out3}}, decoder_2_out3};  // Bit_Extender bit_extender_2
  assign bit_extender_3_out = {{2{decoder_2_out1}}, decoder_2_out1};  // Bit_Extender bit_extender_3
  assign bit_extender_4_out = {{2{decoder_2_out2}}, decoder_2_out2};  // Bit_Extender bit_extender_4
  or or_19 (out_44, and_23_out, and_24_out);
  assign and_25_out = in_7 & bit_extender_1_out;  // AND_Gate and_25, 3 bits wide
  assign and_26_out = in_8 & bit_extender_3_out;  // AND_Gate and_26, 3 bits wide
  assign and_27_out = bit_extender_4_out & in_10;  // AND_Gate and_27, 3 bits wide
  assign and_28_out = bit_extender_2_out & in_11;  // AND_Gate and_28, 3 bits wide
  Decoder #(.enable("false"), .select(4)) decoder_3 (
    .out0(decoder_3_out0), .out1(decoder_3_out1), .out2(decoder_3_out2), .out3(decoder_3_out3),
    .out4(decoder_3_out4), .out5(decoder_3_out5), .out6(decoder_3_out6), .out7(decoder_3_out7),
    .out8(decoder_3_out8), .out9(decoder_3_out9), .out10(decoder_3_out10), .out11(decoder_3_out11),
    .out12(decoder_3_out12), .out13(decoder_3_out13), .out14(decoder_3_out14), .out15(decoder_3_out15),
    .sel(in_16));
  assign out_50 = and_25_out | and_26_out | and_27_out | and_28_out;  // OR_Gate or_20, 3 bits wide
  Half_suber half_suber_1 (.A(A), .B(B), .D(half_suber_1_d), .Bo(half_suber_1_bo));
  // DipSwitch #(.number(5)) dipswitch_2: pin names not known; wires that end beside it: dipswitch_2_p1
  assign bit_extender_5_out = {{3{not_16_out}}, not_16_out};  // Bit_Extender bit_extender_5
  not not_16 (not_16_out, dipswitch_2_p1);
  assign bit_extender_6_out = {{3{dipswitch_2_p1}}, dipswitch_2_p1};  // Bit_Extender bit_extender_6
  Half_suber half_suber_2 (.A(half_suber_1_d), .B(Bin), .D(D), .Bo(half_suber_2_bo));
  // DipSwitch #(.number(4)) dipswitch_3: pin names not known; wires that end beside it: dipswitch_3_p4[3], dipswitch_3_p4[2], dipswitch_3_p4[1], dipswitch_3_p4[0]
  assign bit_extender_7_out = {{3{in_39[3]}}, in_39[3]};  // Bit_Extender bit_extender_7
  assign and_29_out = undriven & bit_extender_5_out;  // AND_Gate and_29, 4 bits wide
  assign and_30_out = undriven & bit_extender_6_out;  // AND_Gate and_30, 4 bits wide
  or or_21 (or_21_out, decoder_3_out10, decoder_3_out12, decoder_3_out0, decoder_3_out2, decoder_3_out3, decoder_3_out9, decoder_3_out5, decoder_3_out6, decoder_3_out7, decoder_3_out8, decoder_3_out14, decoder_3_out15);
  or or_22 (Bout, half_suber_2_bo, half_suber_1_bo);
  seven_segment_circuit16 seven_segment_circuit16_2 (
    .in_1(dipswitch_3_p4), .a(seven_segment_circuit16_2_a), .b(seven_segment_circuit16_2_b),
    .c(seven_segment_circuit16_2_c), .d(seven_segment_circuit16_2_d), .e(seven_segment_circuit16_2_e),
    .f(seven_segment_circuit16_2_f), .g(seven_segment_circuit16_2_g));
  seven_segment_circuit16 seven_segment_circuit16_3 (
    .in_1(dipswitch_4_p4), .a(seven_segment_circuit16_3_a), .b(seven_segment_circuit16_3_b),
    .c(seven_segment_circuit16_3_c), .d(seven_segment_circuit16_3_d), .e(seven_segment_circuit16_3_e),
    .f(seven_segment_circuit16_3_f), .g(seven_segment_circuit16_3_g));
  not not_17 (not_17_out[0], in_38[0]);
  not not_18 (not_17_out[1], in_38[1]);
  not not_19 (not_17_out[2], in_38[2]);
  assign and_31_out = {in_38[3], not_17_out} & bit_extender_8_out;  // AND_Gate and_31, 4 bits wide
  assign bit_extender_8_out = {{3{in_38[3]}}, in_38[3]};  // Bit_Extender bit_extender_8
  assign not_20_out = ~bit_extender_7_out;  // NOT_Gate not_20, 4 bits wide
  not not_21 (not_23_out[2], in_39[2]);
  not not_22 (not_23_out[1], in_39[1]);
  not not_23 (not_23_out[0], in_39[0]);
  or or_23 (or_23_out, decoder_3_out10, decoder_3_out0, decoder_3_out1, decoder_3_out2, decoder_3_out3, decoder_3_out4, decoder_3_out8, decoder_3_out7, decoder_3_out9, decoder_3_out13);
  _7_Segment_Display u_7_segment_display_3 (
    .g(seven_segment_circuit16_2_g), .f(seven_segment_circuit16_2_f), .a(seven_segment_circuit16_2_a),
    .b(seven_segment_circuit16_2_b), .e(seven_segment_circuit16_2_e), .d(seven_segment_circuit16_2_d),
    .c(seven_segment_circuit16_2_c));  // open: dp
  _7_Segment_Display u_7_segment_display_4 (
    .g(seven_segment_circuit16_3_g), .f(seven_segment_circuit16_3_f), .a(seven_segment_circuit16_3_a),
    .b(seven_segment_circuit16_3_b), .e(seven_segment_circuit16_3_e), .d(seven_segment_circuit16_3_d),
    .c(seven_segment_circuit16_3_c));  // open: dp
  adder_4 adder_4_1 (.A(in_36), .B(in_37), .S(adder_4_1_s));  // open: Cout
  assign not_24_out = ~bit_extender_8_out;  // NOT_Gate not_24, 4 bits wide
  assign and_32_out = not_24_out & in_38;  // AND_Gate and_32, 4 bits wide
  assign and_33_out = in_39 & not_20_out;  // AND_Gate and_33, 4 bits wide
  assign and_34_out = bit_extender_7_out & {in_39[3], not_23_out};  // AND_Gate and_34, 4 bits wide
  or or_24 (or_24_out, decoder_3_out5, decoder_3_out10, decoder_3_out0, decoder_3_out1, decoder_3_out3, decoder_3_out4, decoder_3_out6, decoder_3_out7, decoder_3_out8, decoder_3_out9, decoder_3_out11, decoder_3_out13);
  // DipSwitch #(.number(4)) dipswitch_4: pin names not known; wires that end beside it: dipswitch_4_p4[3], dipswitch_4_p4[2], dipswitch_4_p4[1], dipswitch_4_p4[0]
  assign or_25_out = and_31_out | and_32_out;  // OR_Gate or_25, 4 bits wide
  assign or_26_out = and_33_out | and_34_out;  // OR_Gate or_26, 4 bits wide
  adder_4 adder_4_2 (.A(in_40), .B(in_41), .Cout(adder_4_2_cout[0]), .S(adder_4_2_s));
  or or_27 (or_27_out, decoder_3_out11, decoder_3_out12, decoder_3_out0, decoder_3_out2, decoder_3_out3, decoder_3_out5, decoder_3_out6, decoder_3_out8, decoder_3_out9, decoder_3_out13, decoder_3_out14);
  Half_suber half_suber_3 (.A(dipswitch_3_p4[0]), .B(dipswitch_4_p4[0]), .D(half_suber_3_d[0]), .Bo(half_suber_3_bo));
  suber_4 suber_4_1 (.B({1'b0, in_37[2:0]}), .A({1'b0, in_36[2:0]}), .Bout(suber_4_1_bout), .D(suber_4_1_d));
  suber_4 suber_4_2 (.B({1'b0, in_36[2:0]}), .A({1'b0, in_37[2:0]}), .Bout(suber_4_2_bout), .D(suber_4_2_d));
  seven_segment_circuit10 seven_segment_circuit10_1 (
    .in_1(and_29_out), .out_2(seven_segment_circuit10_1_out_2), .out_3(seven_segment_circuit10_1_out_3),
    .out_4(seven_segment_circuit10_1_out_4), .out_5(seven_segment_circuit10_1_out_5),
    .out_6(seven_segment_circuit10_1_out_6), .out_7(seven_segment_circuit10_1_out_7),
    .out_8(seven_segment_circuit10_1_out_8), .out_9(seven_segment_circuit10_1_out_9));
  seven_segment_circuit16 seven_segment_circuit16_4 (
    .in_1(and_30_out), .a(seven_segment_circuit16_4_a), .b(seven_segment_circuit16_4_b),
    .c(seven_segment_circuit16_4_c), .d(seven_segment_circuit16_4_d), .e(seven_segment_circuit16_4_e),
    .f(seven_segment_circuit16_4_f), .g(seven_segment_circuit16_4_g));
  or or_28 (or_28_out, decoder_3_out10, decoder_3_out11, decoder_3_out12, decoder_3_out0, decoder_3_out2, decoder_3_out6, decoder_3_out8, decoder_3_out13, decoder_3_out14, decoder_3_out15);
  _7_Segment_Display u_7_segment_display_5 (
    .g(seven_segment_circuit16_4_g), .f(seven_segment_circuit16_4_f), .a(seven_segment_circuit16_4_a),
    .b(seven_segment_circuit16_4_b), .e(seven_segment_circuit16_4_e), .d(seven_segment_circuit16_4_d),
    .c(seven_segment_circuit16_4_c));  // open: dp
  or or_29 (or_29_out, decoder_3_out10, decoder_3_out11, decoder_3_out0, decoder_3_out4, decoder_3_out5, decoder_3_out12, decoder_3_out6, decoder_3_out8, decoder_3_out9, decoder_3_out14, decoder_3_out15);
  LED led_1 (.in(full_suber_3_bout));
  decoder2_4 decoder2_4_5 (
    .in_1(in_36[3]), .in_2(in_37[3]), .out_3(decoder2_4_5_out_3), .out_4(decoder2_4_5_out_4),
    .out_5(decoder2_4_5_out_5), .out_6(decoder2_4_5_out_6));
  assign bit_extender_9_out = {{3{suber_4_1_bout}}, suber_4_1_bout};  // Bit_Extender bit_extender_9
  assign and_35_out = bit_extender_9_out & suber_4_2_d;  // AND_Gate and_35, 4 bits wide
  assign and_36_out = suber_4_1_d & bit_extender_10_out;  // AND_Gate and_36, 4 bits wide
  assign bit_extender_10_out = {{3{suber_4_2_bout}}, suber_4_2_bout};  // Bit_Extender bit_extender_10
  and and_37 (and_37_out, suber_4_2_bout, in_36[3]);
  Sign_magnitude_adder_4bit sign_magnitude_adder_4bit_1 (
    .in_1(or_25_out), .in_2(or_26_out), .O0(sign_magnitude_adder_4bit_1_o0[0]),
    .O1(sign_magnitude_adder_4bit_1_o0[1]), .O2(sign_magnitude_adder_4bit_1_o0[2]),
    .S(sign_magnitude_adder_4bit_1_s));
  or or_30 (or_30_out, decoder_3_out5, decoder_3_out10, decoder_3_out11, decoder_3_out2, decoder_3_out3, decoder_3_out4, decoder_3_out6, decoder_3_out8, decoder_3_out9, decoder_3_out13, decoder_3_out14, decoder_3_out15);
  and and_38 (and_38_out, suber_4_1_bout, in_37[3]);
  adder_4 adder_4_3 (.A({3'b000, adder_4_2_cout[0]}), .B(adder_4_2_s), .S(adder_4_3_s));  // open: Cout
  _7_Segment_Display u_7_segment_display_6 (
    .g(seven_segment_circuit10_1_out_8), .f(seven_segment_circuit10_1_out_7),
    .a(seven_segment_circuit10_1_out_2), .b(seven_segment_circuit10_1_out_3),
    .e(seven_segment_circuit10_1_out_6), .d(seven_segment_circuit10_1_out_5),
    .c(seven_segment_circuit10_1_out_4), .dp(seven_segment_circuit10_1_out_9));
  _7_Segment_Display u_7_segment_display_7 (
    .g(or_30_out), .f(or_29_out), .a(or_21_out), .b(or_23_out), .e(or_28_out), .d(or_27_out), .c(or_24_out));  // open: dp
  Full_suber full_suber_1 (
    .Bin(half_suber_3_bo), .A(dipswitch_3_p4[1]), .B(dipswitch_4_p4[1]), .D(half_suber_3_d[1]),
    .Bout(full_suber_1_bout));
  assign and_39_out = {1'b1, adder_4_1_s[2:0]} & bit_extender_11_out;  // AND_Gate and_39, 4 bits wide
  assign bit_extender_11_out = {{3{decoder2_4_5_out_6}}, decoder2_4_5_out_6};  // Bit_Extender bit_extender_11
  assign bit_extender_12_out = {{3{decoder2_4_5_out_3}}, decoder2_4_5_out_3};  // Bit_Extender bit_extender_12
  or or_31 (or_31_out, decoder2_4_5_out_4, decoder2_4_5_out_5);
  not not_25 (not_25_out[0], adder_4_3_s[0]);
  not not_26 (not_25_out[1], adder_4_3_s[1]);
  not not_27 (not_25_out[2], adder_4_3_s[2]);
  assign bit_extender_13_out = {{3{adder_4_3_s[3]}}, adder_4_3_s[3]};  // Bit_Extender bit_extender_13
  assign and_40_out = {1'b0, adder_4_1_s[2:0]} & bit_extender_12_out;  // AND_Gate and_40, 4 bits wide
  assign and_41_out = bit_extender_14_out & {or_33_out[3], or_32_out[2:0]};  // AND_Gate and_41, 4 bits wide
  assign bit_extender_14_out = {{3{or_31_out}}, or_31_out};  // Bit_Extender bit_extender_14
  assign or_32_out = and_35_out | and_36_out;  // OR_Gate or_32, 4 bits wide
  or or_33 (or_33_out[3], and_37_out, and_38_out);
  assign and_42_out = {adder_4_3_s[3], not_25_out} & bit_extender_13_out;  // AND_Gate and_42, 4 bits wide
  assign not_28_out = ~bit_extender_13_out;  // NOT_Gate not_28, 4 bits wide
  seven_segment_circuit16 seven_segment_circuit16_5 (
    .in_1(half_suber_3_d), .a(seven_segment_circuit16_5_a), .b(seven_segment_circuit16_5_b),
    .c(seven_segment_circuit16_5_c), .d(seven_segment_circuit16_5_d), .e(seven_segment_circuit16_5_e),
    .f(seven_segment_circuit16_5_f), .g(seven_segment_circuit16_5_g));
  assign out_64 = and_39_out | and_40_out | and_41_out;  // OR_Gate or_34, 4 bits wide
  seven_segment_circuit16 seven_segment_circuit16_6 (
    .in_1({1'b0, sign_magnitude_adder_4bit_1_o0}), .a(seven_segment_circuit16_6_a),
    .b(seven_segment_circuit16_6_b), .c(seven_segment_circuit16_6_c), .d(seven_segment_circuit16_6_d),
    .e(seven_segment_circuit16_6_e), .f(seven_segment_circuit16_6_f), .g(seven_segment_circuit16_6_g));
  _7_Segment_Display u_7_segment_display_8 (.g(sign_magnitude_adder_4bit_1_s));  // open: f, a, b, e, d, c, dp
  assign and_43_out = not_28_out & adder_4_3_s;  // AND_Gate and_43, 4 bits wide
  Full_suber full_suber_2 (
    .Bin(full_suber_1_bout), .A(dipswitch_3_p4[2]), .B(dipswitch_4_p4[2]), .D(half_suber_3_d[2]),
    .Bout(full_suber_2_bout));
  _7_Segment_Display u_7_segment_display_9 (
    .g(seven_segment_circuit16_5_g), .f(seven_segment_circuit16_5_f), .a(seven_segment_circuit16_5_a),
    .b(seven_segment_circuit16_5_b), .e(seven_segment_circuit16_5_e), .d(seven_segment_circuit16_5_d),
    .c(seven_segment_circuit16_5_c));  // open: dp
  _7_Segment_Display u_7_segment_display_10 (
    .g(seven_segment_circuit16_6_g), .f(seven_segment_circuit16_6_f), .a(seven_segment_circuit16_6_a),
    .b(seven_segment_circuit16_6_b), .e(seven_segment_circuit16_6_e), .d(seven_segment_circuit16_6_d),
    .c(seven_segment_circuit16_6_c));  // open: dp
  assign {or_35_out_2[3], or_35_out} = and_42_out | and_43_out;  // OR_Gate or_35, 4 bits wide
  // DipSwitch #(.number(4)) dipswitch_5: pin names not known; wires that end beside it: dipswitch_5_p1, dipswitch_5_p2, dipswitch_5_p3
  // DipSwitch #(.number(4)) dipswitch_6: pin names not known; wires that end beside it: dipswitch_6_p1, dipswitch_6_p2, dipswitch_6_p3, dipswitch_6_p4, dipswitch_6_p5
  // DipSwitch #(.number(4)) dipswitch_7: pin names not known; wires that end beside it: dipswitch_7_p1, dipswitch_7_p2, dipswitch_7_p3, dipswitch_7_p4
  seven_segment_circuit16 seven_segment_circuit16_7 (
    .in_1({1'b0, or_35_out}), .a(seven_segment_circuit16_7_a), .b(seven_segment_circuit16_7_b),
    .c(seven_segment_circuit16_7_c), .d(seven_segment_circuit16_7_d), .e(seven_segment_circuit16_7_e),
    .f(seven_segment_circuit16_7_f), .g(seven_segment_circuit16_7_g));
  _7_Segment_Display u_7_segment_display_11 (.g(or_35_out_2[3]));  // open: f, a, b, e, d, c, dp
  _7_Segment_Display u_7_segment_display_12 (
    .g(seven_segment_circuit16_7_g), .f(seven_segment_circuit16_7_f), .a(seven_segment_circuit16_7_a),
    .b(seven_segment_circuit16_7_b), .e(seven_segment_circuit16_7_e), .d(seven_segment_circuit16_7_d),
    .c(seven_segment_circuit16_7_c));  // open: dp
  // DipSwitch #(.number(4)) dipswitch_8: pin names not known; wires that end beside it: dipswitch_8_p1, dipswitch_8_p2, dipswitch_8_p3, dipswitch_8_p4
  xnor xnor_1 (xnor_1_out, dipswitch_5_p1, dipswitch_6_p2);
  xnor xnor_2 (xnor_2_out, dipswitch_5_p2, dipswitch_6_p3);
  xnor xnor_3 (xnor_3_out, dipswitch_5_p3, dipswitch_6_p4);
  xnor xnor_4 (xnor_4_out, dipswitch_6_p1, dipswitch_6_p5);
  seven_segment_circuit16 seven_segment_circuit16_8 (
    .in_1({1'b0, out_64[2:0]}), .a(seven_segment_circuit16_8_a), .b(seven_segment_circuit16_8_b),
    .c(seven_segment_circuit16_8_c), .d(seven_segment_circuit16_8_d), .e(seven_segment_circuit16_8_e),
    .f(seven_segment_circuit16_8_f), .g(seven_segment_circuit16_8_g));
  _7_Segment_Display u_7_segment_display_13 (.g(out_64[3]));  // open: f, a, b, e, d, c, dp
  _7_Segment_Display u_7_segment_display_14 (
    .g(seven_segment_circuit16_8_g), .f(seven_segment_circuit16_8_f), .a(seven_segment_circuit16_8_a),
    .b(seven_segment_circuit16_8_b), .e(seven_segment_circuit16_8_e), .d(seven_segment_circuit16_8_d),
    .c(seven_segment_circuit16_8_c));  // open: dp
  Full_suber full_suber_3 (
    .Bin(full_suber_2_bout), .A(dipswitch_3_p4[3]), .B(dipswitch_4_p4[3]), .D(half_suber_3_d[3]),
    .Bout(full_suber_3_bout));
  and and_44 (and_44_out, xnor_1_out, xnor_2_out, xnor_3_out, xnor_4_out);
  LED led_2 (.in(and_44_out));
  Half_adder half_adder_1 (.in_1(in_12), .in_2(in_13), .S(half_adder_1_s), .C(half_adder_1_c));
  Half_adder half_adder_2 (.in_1(dipswitch_8_p4), .in_2(dipswitch_7_p4), .S(half_adder_2_s[0]), .C(half_adder_2_c));
  Half_adder half_adder_3 (.in_1(half_adder_1_s), .in_2(in_14), .S(out_53), .C(half_adder_3_c));
  Full_Adder full_adder_1 (
    .Cin(half_adder_2_c), .A(dipswitch_8_p3), .B(dipswitch_7_p3), .Cout(full_adder_1_cout),
    .S(half_adder_2_s[1]));
  or or_36 (out_52, half_adder_1_c, half_adder_3_c);
  seven_segment_circuit16 seven_segment_circuit16_9 (
    .in_1(half_adder_2_s), .a(seven_segment_circuit16_9_a), .b(seven_segment_circuit16_9_b),
    .c(seven_segment_circuit16_9_c), .d(seven_segment_circuit16_9_d), .e(seven_segment_circuit16_9_e),
    .f(seven_segment_circuit16_9_f), .g(seven_segment_circuit16_9_g));
  Full_Adder full_adder_2 (
    .Cin(full_adder_1_cout), .A(dipswitch_8_p2), .B(dipswitch_7_p2), .Cout(full_adder_2_cout),
    .S(half_adder_2_s[2]));
  _7_Segment_Display u_7_segment_display_15 (
    .g(seven_segment_circuit16_9_g), .f(seven_segment_circuit16_9_f), .a(seven_segment_circuit16_9_a),
    .b(seven_segment_circuit16_9_b), .e(seven_segment_circuit16_9_e), .d(seven_segment_circuit16_9_d),
    .c(seven_segment_circuit16_9_c));  // open: dp
  LED led_3 (.in(full_adder_3_cout));
  Full_Adder full_adder_3 (
    .Cin(full_adder_2_cout), .A(dipswitch_8_p1), .B(dipswitch_7_p1), .Cout(full_adder_3_cout),
    .S(half_adder_2_s[3]));

  // Notes on the sheet:
  //   七段数码管译码器1
  //   2-4译码器实现3-8译码器
  //   16-4编码器
  //   1位2选1选择器
  //   3位4选1选择器
  //   七段数码管译码器2
  //   半减器实现的全减器
  //   可切换进位计数制的七段数码管
  //   4位原码加法器
  //   A
  //   B
  //   A
  //   B
  //   B
  //   4位反码加法器
  //   A
  //   A
  //   绝对值进行减法
  //   A的符号位
  //   B的符号位
  //   4位反码加法器2
  //   B
  //   A-B
  //   B-A
  //   Bout1代表A绝对值大，结果选另一个
  //   Bout1代表B绝对值大，结果选另一个
  //   4位减法器
  //   这里可以获得大绝对值-小绝对值的无符号结果
  //   异号
  //   绝对值大的符号位
  //   4位比较器
  //   通过半加器实现的全加器
endmodule

module decoder2_4 (
  input  in_1,
  input  in_2,
  output out_3,
  output out_4,
  output out_5,
  output out_6
);

  wire not_1_out, not_2_out;

  not not_1 (not_1_out, in_1);
  not not_2 (not_2_out, in_2);
  and and_1 (out_3, not_1_out, not_2_out);
  and and_2 (out_4, not_1_out, in_2);
  and and_3 (out_5, in_1, not_2_out);
  and and_4 (out_6, in_1, in_2);

  // Notes on the sheet:
  //   2-4译码器
endmodule

module seven_segment_circuit16 (
  input  [3:0] in_1,
  output a,
  output b,
  output c,
  output d,
  output e,
  output f,
  output g
);

  wire decoder_1_out0, decoder_1_out1, decoder_1_out2, decoder_1_out3, decoder_1_out4, decoder_1_out5,
       decoder_1_out6, decoder_1_out7, decoder_1_out8, decoder_1_out9, decoder_1_out10, decoder_1_out11,
       decoder_1_out12, decoder_1_out13, decoder_1_out14, decoder_1_out15;

  Decoder #(.enable("false"), .select(4)) decoder_1 (
    .out0(decoder_1_out0), .out1(decoder_1_out1), .out2(decoder_1_out2), .out3(decoder_1_out3),
    .out4(decoder_1_out4), .out5(decoder_1_out5), .out6(decoder_1_out6), .out7(decoder_1_out7),
    .out8(decoder_1_out8), .out9(decoder_1_out9), .out10(decoder_1_out10), .out11(decoder_1_out11),
    .out12(decoder_1_out12), .out13(decoder_1_out13), .out14(decoder_1_out14), .out15(decoder_1_out15),
    .sel(in_1));
  or or_1 (a, decoder_1_out10, decoder_1_out12, decoder_1_out0, decoder_1_out2, decoder_1_out3, decoder_1_out9, decoder_1_out5, decoder_1_out6, decoder_1_out7, decoder_1_out8, decoder_1_out14, decoder_1_out15);
  or or_2 (b, decoder_1_out10, decoder_1_out0, decoder_1_out1, decoder_1_out2, decoder_1_out3, decoder_1_out4, decoder_1_out8, decoder_1_out7, decoder_1_out9, decoder_1_out13);
  or or_3 (c, decoder_1_out5, decoder_1_out10, decoder_1_out0, decoder_1_out1, decoder_1_out3, decoder_1_out4, decoder_1_out6, decoder_1_out7, decoder_1_out8, decoder_1_out9, decoder_1_out11, decoder_1_out13);
  or or_4 (d, decoder_1_out11, decoder_1_out12, decoder_1_out0, decoder_1_out2, decoder_1_out3, decoder_1_out5, decoder_1_out6, decoder_1_out8, decoder_1_out9, decoder_1_out13, decoder_1_out14);
  or or_5 (e, decoder_1_out10, decoder_1_out11, decoder_1_out12, decoder_1_out0, decoder_1_out2, decoder_1_out6, decoder_1_out8, decoder_1_out13, decoder_1_out14, decoder_1_out15);
  or or_6 (f, decoder_1_out10, decoder_1_out11, decoder_1_out0, decoder_1_out4, decoder_1_out5, decoder_1_out12, decoder_1_out6, decoder_1_out8, decoder_1_out9, decoder_1_out14, decoder_1_out15);
  or or_7 (g, decoder_1_out5, decoder_1_out10, decoder_1_out11, decoder_1_out2, decoder_1_out3, decoder_1_out4, decoder_1_out6, decoder_1_out8, decoder_1_out9, decoder_1_out13, decoder_1_out14, decoder_1_out15);

  // Notes on the sheet:
  //   七段数码管译码器2
endmodule

module encoder16_4 (
  input  in_1,
  input  in_2,
  input  in_3,
  input  in_4,
  input  in_5,
  input  in_6,
  input  in_7,
  input  in_8,
  input  in_9,
  input  in_10,
  input  in_11,
  input  in_12,
  input  in_13,
  input  in_14,
  input  in_15,
  input  in_16,
  output out_17,
  output out_18,
  output out_19,
  output out_20
);

  or low1 (out_17, in_2, in_4, in_6, in_8, in_10, in_12, in_14, in_16);
  or or_1 (out_18, in_3, in_4, in_7, in_8, in_11, in_12, in_15, in_16);
  or or_2 (out_19, in_5, in_6, in_7, in_8, in_13, in_14, in_15, in_16);
  or high1 (out_20, in_9, in_10, in_11, in_12, in_13, in_14, in_15, in_16);
endmodule

module priority_encoder4_2 (
  input  \_4_2优先编码器 ,
  input  in_2,
  input  in_3,
  input  in_4,
  output out_5,
  output out_6
);

  wire and_1_out, and_2_out, not_1_out, not_2_out, not_3_out;

  not not_1 (not_1_out, in_3);
  not not_2 (not_2_out, in_4);
  not not_3 (not_3_out, in_4);
  and and_1 (and_1_out, in_2, not_1_out, not_2_out);
  and and_2 (and_2_out, in_3, not_3_out);
  or or_1 (out_5, in_4, and_1_out);
  or or_2 (out_6, and_2_out, in_4);
endmodule

module seven_segment_circuit10 (
  input  [3:0] in_1,
  output out_2,
  output out_3,
  output out_4,
  output out_5,
  output out_6,
  output out_7,
  output out_8,
  output out_9
);

  wire decoder_1_out0, decoder_1_out1, decoder_1_out2, decoder_1_out3, decoder_1_out4, decoder_1_out5,
       decoder_1_out6, decoder_1_out7, decoder_1_out8, decoder_1_out9, decoder_1_out10, decoder_1_out11,
       decoder_1_out12, decoder_1_out13, decoder_1_out14, decoder_1_out15;

  Decoder #(.enable("false"), .select(4)) decoder_1 (
    .out0(decoder_1_out0), .out1(decoder_1_out1), .out2(decoder_1_out2), .out3(decoder_1_out3),
    .out4(decoder_1_out4), .out5(decoder_1_out5), .out6(decoder_1_out6), .out7(decoder_1_out7),
    .out8(decoder_1_out8), .out9(decoder_1_out9), .out10(decoder_1_out10), .out11(decoder_1_out11),
    .out12(decoder_1_out12), .out13(decoder_1_out13), .out14(decoder_1_out14), .out15(decoder_1_out15),
    .sel(in_1));
  or or_1 (out_9, decoder_1_out15, decoder_1_out14, decoder_1_out13, decoder_1_out12, decoder_1_out11, decoder_1_out10);
  or or_2 (out_2, decoder_1_out0, decoder_1_out2, decoder_1_out3, decoder_1_out9, decoder_1_out5, decoder_1_out6, decoder_1_out7, decoder_1_out8);
  or or_3 (out_3, decoder_1_out0, decoder_1_out1, decoder_1_out2, decoder_1_out3, decoder_1_out4, decoder_1_out8, decoder_1_out7, decoder_1_out9);
  or or_4 (out_4, decoder_1_out0, decoder_1_out1, decoder_1_out3, decoder_1_out4, decoder_1_out5, decoder_1_out6, decoder_1_out7, decoder_1_out8, decoder_1_out9);
  or or_5 (out_5, decoder_1_out0, decoder_1_out2, decoder_1_out3, decoder_1_out5, decoder_1_out6, decoder_1_out8, decoder_1_out9);
  or or_6 (out_6, decoder_1_out0, decoder_1_out2, decoder_1_out6, decoder_1_out8);
  or or_7 (out_7, decoder_1_out0, decoder_1_out4, decoder_1_out5, decoder_1_out6, decoder_1_out8, decoder_1_out9);
  or or_8 (out_8, decoder_1_out2, decoder_1_out3, decoder_1_out4, decoder_1_out5, decoder_1_out6, decoder_1_out8, decoder_1_out9);

  // Notes on the sheet:
  //   七段数码管译码器1
endmodule

module Half_adder (
  input  in_1,
  input  in_2,
  output S,
  output C
);

  xor xor_1 (S, in_1, in_2);
  and and_1 (C, in_1, in_2);
endmodule

module Full_Adder (
  input  Cin,
  input  A,
  input  B,
  output Cout,
  output S
);

  wire and_1_out, and_2_out, or_1_out;

  and and_1 (and_1_out, A, B);
  and and_2 (and_2_out, Cin, or_1_out);
  or or_1 (or_1_out, B, A);
  xor xor_1 (S, Cin, A, B);
  or or_2 (Cout, and_2_out, and_1_out);
endmodule

module Half_suber (
  input  A,
  input  B,
  output D,
  output Bo
);

  wire not_1_out;

  not not_1 (not_1_out, A);
  xor xor_1 (D, A, B);
  and and_1 (Bo, not_1_out, B);
endmodule

module Full_suber (
  input  Bin,
  input  A,
  input  B,
  output D,
  output Bout
);

  wire and_1_out, and_2_out, and_3_out, not_1_out, not_2_out, or_1_out;

  not not_1 (not_1_out, Bin);
  not not_2 (not_2_out, A);
  xor xor_1 (D, Bin, A, B);
  and and_1 (and_1_out, not_2_out, B);
  or or_1 (or_1_out, not_2_out, B);
  and and_2 (and_2_out, not_1_out, and_1_out);
  and and_3 (and_3_out, or_1_out, Bin);
  or or_2 (Bout, and_2_out, and_3_out);
endmodule

module suber_4 (
  input  [3:0] B,
  input  [3:0] A,
  output Bout,
  output [3:0] D
);

  wire full_suber_1_bout, full_suber_2_bout, half_suber_1_bo;

  Half_suber half_suber_1 (.A(A[0]), .B(B[0]), .D(D[0]), .Bo(half_suber_1_bo));
  Full_suber full_suber_1 (.Bin(half_suber_1_bo), .A(A[1]), .B(B[1]), .D(D[1]), .Bout(full_suber_1_bout));
  Full_suber full_suber_2 (.Bin(full_suber_1_bout), .A(A[2]), .B(B[2]), .D(D[2]), .Bout(full_suber_2_bout));
  Full_suber full_suber_3 (.Bin(full_suber_2_bout), .A(A[3]), .B(B[3]), .D(D[3]), .Bout(Bout));

  // Notes on the sheet:
  //   B
endmodule

module adder_4 (
  input  [3:0] A,
  input  [3:0] B,
  output Cout,
  output [3:0] S
);

  wire full_adder_1_cout, full_adder_2_cout, half_adder_1_c;

  Half_adder half_adder_1 (.in_1(B[0]), .in_2(A[0]), .S(S[0]), .C(half_adder_1_c));
  Full_Adder full_adder_1 (.Cin(half_adder_1_c), .A(B[1]), .B(A[1]), .Cout(full_adder_1_cout), .S(S[1]));
  Full_Adder full_adder_2 (.Cin(full_adder_1_cout), .A(B[2]), .B(A[2]), .Cout(full_adder_2_cout), .S(S[2]));
  Full_Adder full_adder_3 (.Cin(full_adder_2_cout), .A(B[3]), .B(A[3]), .Cout(Cout), .S(S[3]));
endmodule

module Sign_magnitude_adder_4bit (
  input  [3:0] in_1,
  input  [3:0] in_2,
  output O0,
  output O1,
  output O2,
  output S
);

  wire and_1_out, and_4_out, decoder2_4_1_out_3, decoder2_4_1_out_4, decoder2_4_1_out_5, decoder2_4_1_out_6,
       or_1_out, suber_4_1_bout, suber_4_2_bout;
  wire [3:0] adder_4_1_s, and_2_out, and_3_out, and_5_out, and_6_out, and_7_out, bit_extender_1_out,
       bit_extender_2_out, bit_extender_3_out, bit_extender_4_out, bit_extender_5_out, or_2_out, suber_4_1_d,
       suber_4_2_d;
  wire [3:3] or_3_out;

  adder_4 adder_4_1 (.A(in_1), .B(in_2), .S(adder_4_1_s));  // open: Cout
  suber_4 suber_4_1 (.B({1'b0, in_2[2:0]}), .A({1'b0, in_1[2:0]}), .Bout(suber_4_1_bout), .D(suber_4_1_d));
  suber_4 suber_4_2 (.B({1'b0, in_1[2:0]}), .A({1'b0, in_2[2:0]}), .Bout(suber_4_2_bout), .D(suber_4_2_d));
  assign bit_extender_1_out = {{3{suber_4_1_bout}}, suber_4_1_bout};  // Bit_Extender bit_extender_1
  assign bit_extender_2_out = {{3{suber_4_2_bout}}, suber_4_2_bout};  // Bit_Extender bit_extender_2
  and and_1 (and_1_out, suber_4_2_bout, in_1[3]);
  decoder2_4 decoder2_4_1 (
    .in_1(in_1[3]), .in_2(in_2[3]), .out_3(decoder2_4_1_out_3), .out_4(decoder2_4_1_out_4),
    .out_5(decoder2_4_1_out_5), .out_6(decoder2_4_1_out_6));
  assign and_2_out = bit_extender_1_out & suber_4_2_d;  // AND_Gate and_2, 4 bits wide
  assign and_3_out = suber_4_1_d & bit_extender_2_out;  // AND_Gate and_3, 4 bits wide
  assign bit_extender_3_out = {{3{decoder2_4_1_out_6}}, decoder2_4_1_out_6};  // Bit_Extender bit_extender_3
  assign bit_extender_4_out = {{3{decoder2_4_1_out_3}}, decoder2_4_1_out_3};  // Bit_Extender bit_extender_4
  or or_1 (or_1_out, decoder2_4_1_out_4, decoder2_4_1_out_5);
  and and_4 (and_4_out, suber_4_1_bout, in_2[3]);
  assign and_5_out = {1'b1, adder_4_1_s[2:0]} & bit_extender_3_out;  // AND_Gate and_5, 4 bits wide
  assign and_6_out = {1'b0, adder_4_1_s[2:0]} & bit_extender_4_out;  // AND_Gate and_6, 4 bits wide
  assign bit_extender_5_out = {{3{or_1_out}}, or_1_out};  // Bit_Extender bit_extender_5
  assign or_2_out = and_2_out | and_3_out;  // OR_Gate or_2, 4 bits wide
  or or_3 (or_3_out[3], and_1_out, and_4_out);
  assign and_7_out = bit_extender_5_out & {or_3_out[3], or_2_out[2:0]};  // AND_Gate and_7, 4 bits wide
  assign {S, O2, O1, O0} = and_5_out | and_6_out | and_7_out;  // OR_Gate or_4, 4 bits wide

  // Notes on the sheet:
  //   A
  //   B
  //   4位原码加法器
  //   绝对值进行减法
  //   A的符号位
  //   B的符号位
  //   Bout1代表B绝对值大，结果选另一个
  //   A-B
  //   B-A
  //   Bout1代表A绝对值大，结果选另一个
  //   这里可以获得大绝对值-小绝对值的无符号结果
  //   异号
  //   绝对值大的符号位
endmodule

module TC_adder_4 (
  input  [3:0] A,
  input  [3:0] B,
  output Cout,
  output [3:0] S,
  output O
);

  wire and_1_out, and_2_out, and_3_out, full_adder_1_cout, full_adder_2_cout, half_adder_1_c, nand_1_out,
       not_1_out;

  and and_1 (and_1_out, A[3], B[3]);
  nand nand_1 (nand_1_out, A[3], B[3]);
  Half_adder half_adder_1 (.in_1(B[0]), .in_2(A[0]), .S(S[0]), .C(half_adder_1_c));
  not not_1 (not_1_out, S[3]);
  and and_2 (and_2_out, S[3], nand_1_out);
  and and_3 (and_3_out, not_1_out, and_1_out);
  or or_1 (O, and_2_out, and_3_out);
  Full_Adder full_adder_1 (.Cin(half_adder_1_c), .A(B[1]), .B(A[1]), .Cout(full_adder_1_cout), .S(S[1]));
  Full_Adder full_adder_2 (.Cin(full_adder_1_cout), .A(B[2]), .B(A[2]), .Cout(full_adder_2_cout), .S(S[2]));
  Full_Adder full_adder_3 (.Cin(full_adder_2_cout), .A(B[3]), .B(A[3]), .Cout(Cout), .S(S[3]));
endmodule
