// Logisim project GateCircuit.circ as structural Verilog: 1 circuit, main circuit main
module main (
  input  A,
  input  B,
  input  in_3,
  input  in_4,
  input  in_5,
  input  in_6,
  input  in_7,
  input  in_8,
  input  in_9,
  input  in_10,
  input  in_11,
  input  in_12,
  input  in_13,
  input  in_14,
  input  in_15,
  input  in_16,
  input  in_17,
  input  in_18,
  input  in_19,
  input  in_20,
  input  in_21,
  output Y,
  output out_23,
  output out_24,
  output out_25,
  output out_26,
  output out_27,
  output out_28,
  output out_29,
  output out_30
);

  wire and_1_out, and_2_out, and_3_out, and_4_out, and_5_out, and_6_out, and_7_out, nor_1_out, not_1_out,
       not_2_out, not_3_out, not_4_out, not_5_out, not_6_out, not_8_out, or_2_out, transistor_1_out,
       transistor_2_out, transistor_7_out, transistor_9_out, transistor_11_out;

  not not_1 (not_1_out, in_3);
  not not_2 (not_2_out, in_6);
  not not_3 (not_3_out, in_12);
  not not_4 (not_4_out, in_13);
  not not_5 (not_5_out, in_17);
  not not_6 (not_6_out, in_18);
  Transistor #(.\type ("n")) transistor_1 (.in(1'b0), .out(transistor_1_out), .gate(A));
  and and_1 (and_1_out, not_1_out, in_6);
  and and_2 (and_2_out, in_3, not_2_out);
  and and_3 (and_3_out, not_3_out, in_13);
  and and_4 (and_4_out, in_12, not_4_out);
  Transistor transistor_2 (.in(1'b1), .out(transistor_2_out), .gate(A));
  Transistor transistor_3 (.in(transistor_2_out), .out(transistor_1_out), .gate(B));
  Transistor #(.\type ("n")) transistor_4 (.in(1'b0), .out(transistor_1_out), .gate(B));
  and and_5 (and_5_out, not_5_out, not_6_out);
  and and_6 (and_6_out, in_17, in_18);
  or or_1 (out_23, and_1_out, and_2_out);
  or or_2 (or_2_out, and_3_out, and_4_out);
  Transistor transistor_5 (.in(1'b1), .out(Y), .gate(transistor_1_out));
  Transistor #(.\type ("n")) transistor_6 (.in(1'b0), .out(Y), .gate(transistor_1_out));
  not not_7 (out_27, or_2_out);
  or or_3 (out_29, and_5_out, and_6_out);
  nor nor_1 (nor_1_out, in_4, in_9);
  and and_7 (and_7_out, in_4, in_9);
  nor nor_2 (out_25, nor_1_out, and_7_out);
  Transistor transistor_7 (.in(1'b1), .out(transistor_7_out), .gate(in_5));
  Transistor #(.\type ("n")) transistor_8 (.in(1'b0), .out(transistor_7_out), .gate(in_5));
  Transistor transistor_9 (.in(1'b1), .out(transistor_9_out), .gate(in_14));
  Transistor #(.\type ("n")) transistor_10 (.in(1'b0), .out(transistor_9_out), .gate(in_14));
  Transistor transistor_11 (.in(1'b1), .out(transistor_11_out), .gate(in_19));
  Transistor #(.\type ("n")) transistor_12 (.in(1'b0), .out(transistor_11_out), .gate(in_19));
  Transistor transistor_13 (.in(in_5), .out(out_24), .gate(in_7));
  Transistor #(.\type ("n")) transistor_14 (.in(transistor_7_out), .out(out_24), .gate(in_7));
  Transistor transistor_15 (.in(in_14), .out(out_28), .gate(in_15));
  Transistor #(.\type ("n")) transistor_16 (.in(transistor_9_out), .out(out_28), .gate(in_15));
  // Transmission_Gate transmission_1: pin names not known; wires that end beside it: out_24, in_5, transistor_7_out, in_8
  // Transmission_Gate transmission_2: pin names not known; wires that end beside it: out_28, in_14, transistor_9_out, in_16
  // Transmission_Gate transmission_3: pin names not known; wires that end beside it: in_20, in_19, transistor_11_out, out_30
  Transistor #(.\type ("n")) transistor_17 (.in(in_19), .out(out_30), .gate(in_21));
  Transistor transistor_18 (.in(transistor_11_out), .out(out_30), .gate(in_21));
  not not_8 (not_8_out, in_10);
  // Transmission_Gate transmission_4: pin names not known; wires that end beside it: out_26, in_10, not_8_out, in_11

  // Notes on the sheet:
  //   或门
  //   异或门
  //   同或门1
  //   同或门2
  //   N1
  //   P1
  //   P2
  //   N2
  //   P3
  //   N3
  //   异或门2
  //   异或门的全定制电路
  //   异或门的全定制电路
  //   同或门的全定制电路
endmodule
