// Logisim project SequentialLogic.circ as structural Verilog: 8 circuits, main circuit main
module main (
  input  RE,
  input  EN,
  input  RE_2,
  input  in_4,
  input  RE_3,
  input  in_6,
  input  in_7,
  input  in_8,
  input  in_9,
  input  D,
  input  RE_4,
  input  RE_5,
  input  in_13,
  input  in_14,
  input  in_15,
  input  EN_2,
  input  D_2,
  input  RE_6,
  input  D_3,
  input  RE_7,
  input  D_4,
  input  EN_3,
  output out_23,
  output out_24,
  output Q,
  output nQ,
  output Q_2,
  output nQ_2,
  output Q_3,
  output nQ_3,
  output nQ_4,
  output out_32,
  output out_33,
  output out_34,
  output out_35,
  output out_36,
  output out_37
);

  wire adder_4_1_cout, adder_8_2_cout, and_1_out, and_2_out, and_3_out, and_4_out, and_5_out, and_6_out,
       and_7_out, and_8_out, and_9_out, and_10_out, and_11_out, and_12_out, and_13_out, and_14_out,
       and_15_out, and_16_out, and_17_out, and_18_out, and_19_out, button_1_out, button_2_out, button_3_out,
       button_4_out, button_5_out, button_6_out, button_7_out, button_8_out, button_9_out, button_10_out,
       clock_1_out, comparator_1_eq, comparator_2_eq, comparator_3_eq, comparator_4_eq, d_ff_1_q, d_ff_2_q,
       d_ff_3_q, d_ff_4_q, d_latch_1_q, d_latch_2_q, d_latch_3_q, d_latch_4_q, d_latch_5_q, d_latch_6_q,
       d_latch_7_q, d_latch_10_q, dipswitch_1_p1, dipswitch_2_p1, dipswitch_3_p1, dipswitch_4_p1,
       dipswitch_5_p1, dipswitch_6_p1, dipswitch_11_p1, dipswitch_12_p1, dipswitch_13_p1, dipswitch_14_p1,
       dipswitch_15_p1, dipswitch_15_p2, dipswitch_15_p3, dipswitch_15_p4, multiplexer_1_out, nor_1_out,
       nor_2_out, nor_3_out, not_1_out, not_2_out, not_3_out, not_4_out, not_5_out, not_6_out, not_7_out,
       not_8_out, not_9_out, not_10_out, not_11_out, not_12_out, not_13_out, not_14_out, not_15_out,
       not_17_out, or_1_out, or_2_out, or_3_out, or_4_out, or_5_out, or_6_out, or_7_out, or_8_out,
       seven_segment_circuit16_1_a, seven_segment_circuit16_1_b, seven_segment_circuit16_1_c,
       seven_segment_circuit16_1_d, seven_segment_circuit16_1_e, seven_segment_circuit16_1_f,
       seven_segment_circuit16_1_g, seven_segment_circuit16_2_a, seven_segment_circuit16_2_b,
       seven_segment_circuit16_2_c, seven_segment_circuit16_2_d, seven_segment_circuit16_2_e,
       seven_segment_circuit16_2_f, seven_segment_circuit16_2_g, seven_segment_circuit16_3_a,
       seven_segment_circuit16_3_b, seven_segment_circuit16_3_c, seven_segment_circuit16_3_d,
       seven_segment_circuit16_3_e, seven_segment_circuit16_3_f, seven_segment_circuit16_3_g,
       seven_segment_circuit16_4_a, seven_segment_circuit16_4_b, seven_segment_circuit16_4_c,
       seven_segment_circuit16_4_d, seven_segment_circuit16_4_e, seven_segment_circuit16_4_f,
       seven_segment_circuit16_4_g, seven_segment_circuit16_5_a, seven_segment_circuit16_5_b,
       seven_segment_circuit16_5_c, seven_segment_circuit16_5_d, seven_segment_circuit16_5_e,
       seven_segment_circuit16_5_f, seven_segment_circuit16_5_g, seven_segment_circuit16_6_a,
       seven_segment_circuit16_6_b, seven_segment_circuit16_6_c, seven_segment_circuit16_6_d,
       seven_segment_circuit16_6_e, seven_segment_circuit16_6_f, seven_segment_circuit16_6_g, sr_latch_3_q,
       undriven;
  wire [3:0] adder_4_1_s, adder_4_2_s, adder_4_3_s, adder_4_4_s, adder_4_5_s, d_flip_flop_1_q,
       multiplexer_2_out, multiplexer_3_out, multiplexer_4_out, register_4_1_o, register_4_2_o,
       register_4_3_o, register_4_4_o, register_4_5_o;
  wire [7:0] adder_8_1_s, adder_8_2_s, register_8_1_o, register_8_2_o;

  // DipSwitch #(.number(1)) dipswitch_1: pin names not known; wires that end beside it: dipswitch_1_p1
  // DipSwitch #(.number(1)) dipswitch_2: pin names not known; wires that end beside it: dipswitch_2_p1
  // DipSwitch #(.number(1)) dipswitch_3: pin names not known; wires that end beside it: dipswitch_3_p1
  // DipSwitch #(.number(1)) dipswitch_4: pin names not known; wires that end beside it: dipswitch_4_p1
  not not_1 (not_1_out, dipswitch_1_p1);
  // DipSwitch #(.number(1)) dipswitch_5: pin names not known; wires that end beside it: dipswitch_5_p1
  // DipSwitch #(.number(1)) dipswitch_6: pin names not known; wires that end beside it: dipswitch_6_p1
  // DipSwitch #(.number(1)) dipswitch_7: pin names not known
  buf and_1 (and_1_out, dipswitch_2_p1);  // AND_Gate
  buf and_2 (and_2_out, dipswitch_2_p1);  // AND_Gate
  // DipSwitch #(.number(1)) dipswitch_8: pin names not known
  // DipSwitch #(.number(1)) dipswitch_9: pin names not known
  buf and_3 (and_3_out, dipswitch_3_p1);  // AND_Gate
  buf and_4 (and_4_out, dipswitch_3_p1);  // AND_Gate
  // DipSwitch #(.number(1)) dipswitch_10: pin names not known
  not not_2 (not_2_out, dipswitch_11_p1);
  // DipSwitch #(.number(1)) dipswitch_11: pin names not known; wires that end beside it: dipswitch_11_p1
  not not_3 (not_3_out, dipswitch_12_p1);
  // DipSwitch #(.number(1)) dipswitch_12: pin names not known; wires that end beside it: dipswitch_12_p1
  not not_4 (not_4_out, button_1_out);
  Button button_1 (.out(button_1_out));
  Button button_2 (.out(button_2_out));
  not not_5 (not_5_out, D);
  Button button_3 (.out(button_3_out));
  not not_6 (not_6_out, not_17_out);
  Button button_4 (.out(button_4_out));
  Button button_5 (.out(button_5_out));
  not not_7 (not_7_out, D_2);
  Button button_6 (.out(button_6_out));
  Button button_7 (.out(button_7_out));
  and and_5 (and_5_out, dipswitch_1_p1, dipswitch_4_p1);
  and and_6 (and_6_out, dipswitch_4_p1, not_1_out);
  and and_7 (and_7_out, dipswitch_5_p1, not_2_out);
  // DipSwitch #(.number(1)) dipswitch_13: pin names not known; wires that end beside it: dipswitch_13_p1
  or or_1 (or_1_out, dipswitch_11_p1, not_8_out);
  not not_8 (not_8_out, dipswitch_5_p1);
  and and_8 (and_8_out, undriven, not_3_out);
  // DipSwitch #(.number(1)) dipswitch_14: pin names not known; wires that end beside it: dipswitch_14_p1
  or or_2 (or_2_out, dipswitch_12_p1, not_9_out);
  not not_9 (not_9_out, undriven);
  not not_10 (not_10_out, button_2_out);
  nor nor_1 (nor_1_out, not_5_out, RE_4);
  not not_11 (not_11_out, button_3_out);
  nor nor_2 (nor_2_out, not_6_out, RE_5);
  not not_12 (not_12_out, button_4_out);
  not not_13 (not_13_out, button_5_out);
  nor nor_3 (nor_3_out, not_7_out, RE_6);
  not not_14 (not_14_out, button_6_out);
  and and_9 (and_9_out, D_3, RE_7);
  not not_15 (not_15_out, button_7_out);
  Multiplexer multiplexer_1 (.in0(out_37), .in1(D_4), .out(multiplexer_1_out), .sel(EN_3));
  nor nor_4 (out_23, and_1_out, out_24);
  nor nor_5 (out_24, out_23, and_2_out);
  nand nand_1 (Q, and_3_out, nQ);
  nand nand_2 (nQ, Q, and_4_out);
  and and_10 (and_10_out, and_7_out, dipswitch_13_p1);
  and and_11 (and_11_out, dipswitch_13_p1, or_1_out);
  and and_12 (and_12_out, and_8_out, dipswitch_14_p1);
  and and_13 (and_13_out, dipswitch_14_p1, or_2_out);
  and and_14 (and_14_out, EN_2, button_5_out);
  SR_Latch sr_latch_1 (.R(and_6_out), .S(and_5_out), .Q(Q_2), .NQ(nQ_2));
  D_Latch d_latch_1 (.WE(not_4_out), .D(in_7), .Q(d_latch_1_q));  // open: NQ
  D_Latch d_latch_2 (.WE(not_10_out), .D(nor_1_out), .Q(d_latch_2_q));  // open: NQ
  D_Latch d_latch_3 (.WE(not_11_out), .D(nor_2_out), .Q(d_latch_3_q));  // open: NQ
  D_Latch d_latch_4 (.WE(button_4_out), .D(in_15), .Q(d_latch_4_q));  // open: NQ
  D_Latch d_latch_5 (.WE(not_13_out), .D(nor_3_out), .Q(d_latch_5_q));  // open: NQ
  D_Latch d_latch_6 (.WE(not_14_out), .D(and_9_out), .Q(d_latch_6_q));  // open: NQ
  D_Latch d_latch_7 (.WE(not_15_out), .D(multiplexer_1_out), .Q(d_latch_7_q));  // open: NQ
  Button button_8 (.out(button_8_out));
  SR_Latch sr_latch_2 (.R(and_11_out), .S(and_10_out), .Q(Q_3), .NQ(nQ_3));
  not not_16 (dipswitch_6_p1, sr_latch_3_q);
  SR_Latch sr_latch_3 (.R(and_13_out), .S(and_12_out), .Q(sr_latch_3_q), .NQ(nQ_4));
  D_Latch d_latch_8 (.WE(button_1_out), .D(d_latch_1_q), .Q(out_32));  // open: NQ
  D_Latch d_latch_9 (.WE(button_2_out), .D(d_latch_2_q), .Q(out_33));  // open: NQ
  not not_17 (not_17_out, d_latch_10_q);
  D_Latch d_latch_10 (.WE(button_3_out), .D(d_latch_3_q), .Q(d_latch_10_q));  // open: NQ
  D_Latch d_latch_11 (.WE(not_12_out), .D(d_latch_4_q), .Q(out_34));  // open: NQ
  D_Latch d_latch_12 (.WE(and_14_out), .D(d_latch_5_q), .Q(out_35));  // open: NQ
  D_Latch d_latch_13 (.WE(button_6_out), .D(d_latch_6_q), .Q(out_36));  // open: NQ
  D_Latch d_latch_14 (.WE(button_7_out), .D(d_latch_7_q), .Q(out_37));  // open: NQ
  D_Flip_Flop d_flip_flop_1 (
    .EN(EN), .clk(button_8_out), .D(dipswitch_15_p1), .RE(RE), .Q(d_flip_flop_1_q[0]));  // open: NQ
  // DipSwitch #(.number(4)) dipswitch_15: pin names not known; wires that end beside it: dipswitch_15_p1, dipswitch_15_p2, dipswitch_15_p3, dipswitch_15_p4
  D_Flip_Flop d_flip_flop_2 (
    .EN(EN), .clk(button_8_out), .D(dipswitch_15_p2), .RE(RE), .Q(d_flip_flop_1_q[1]));  // open: NQ
  or or_3 (or_3_out, RE_2, adder_4_1_cout);
  Button button_9 (.out(button_9_out));
  and and_15 (and_15_out, d_ff_1_q, d_ff_2_q);
  and and_16 (and_16_out, d_ff_2_q, d_ff_1_q, d_ff_3_q);
  and and_17 (and_17_out, d_ff_3_q, d_ff_1_q, d_ff_2_q, d_ff_4_q);
  D_Flip_Flop d_flip_flop_3 (
    .EN(EN), .clk(button_8_out), .D(dipswitch_15_p3), .RE(RE), .Q(d_flip_flop_1_q[2]));  // open: NQ
  or or_4 (or_4_out, RE_3, adder_8_2_cout);
  Button button_10 (.out(button_10_out));
  or or_5 (or_5_out, in_13, d_ff_1_q);
  Clock clock_1 (.out(clock_1_out));
  or or_6 (or_6_out, in_13, and_15_out);
  or or_7 (or_7_out, in_13, and_16_out);
  or or_8 (or_8_out, in_13, and_17_out);
  D_Flip_Flop d_flip_flop_4 (
    .EN(EN), .clk(button_8_out), .D(dipswitch_15_p4), .RE(RE), .Q(d_flip_flop_1_q[3]));  // open: NQ
  seven_segment_circuit16 seven_segment_circuit16_1 (
    .in_1(d_flip_flop_1_q), .a(seven_segment_circuit16_1_a), .b(seven_segment_circuit16_1_b),
    .c(seven_segment_circuit16_1_c), .d(seven_segment_circuit16_1_d), .e(seven_segment_circuit16_1_e),
    .f(seven_segment_circuit16_1_f), .g(seven_segment_circuit16_1_g));
  Register_4 register_4_1 (.D(adder_4_1_s), .RE(or_3_out), .EN(in_4), .clk(button_9_out), .O(register_4_1_o));
  Register_4 register_4_2 (.D(adder_4_2_s), .RE(or_5_out), .EN(in_14), .clk(clock_1_out), .O(register_4_2_o));
  Register_4 register_4_3 (.D(adder_4_3_s), .RE(or_6_out), .EN(in_14), .clk(clock_1_out), .O(register_4_3_o));
  and and_18 (and_18_out, and_19_out, d_ff_3_q);
  seven_segment_circuit16 seven_segment_circuit16_2 (
    .in_1(adder_4_1_s), .a(seven_segment_circuit16_2_a), .b(seven_segment_circuit16_2_b),
    .c(seven_segment_circuit16_2_c), .d(seven_segment_circuit16_2_d), .e(seven_segment_circuit16_2_e),
    .f(seven_segment_circuit16_2_f), .g(seven_segment_circuit16_2_g));
  // Probe on register_8_1_o
  Register_8 register_8_1 (.D(adder_8_2_s), .RE(or_4_out), .EN(in_6), .clk(button_10_out), .O(register_8_1_o));
  // Probe on register_8_2_o
  Multiplexer #(.width(4)) multiplexer_2 (.in0(4'b0000), .in1(4'b0001), .out(multiplexer_2_out), .sel(d_ff_1_q));
  and and_19 (and_19_out, d_ff_1_q, d_ff_2_q);
  Register_4 register_4_4 (.D(adder_4_4_s), .RE(or_7_out), .EN(in_14), .clk(clock_1_out), .O(register_4_4_o));
  Multiplexer #(.width(4)) multiplexer_3 (.in0(4'b0000), .in1(4'b0001), .out(multiplexer_3_out), .sel(and_19_out));
  Register_4 register_4_5 (.D(adder_4_5_s), .RE(or_8_out), .EN(in_14), .clk(clock_1_out), .O(register_4_5_o));
  Multiplexer #(.width(4)) multiplexer_4 (.in0(4'b0000), .in1(4'b0001), .out(multiplexer_4_out), .sel(and_18_out));
  _7_Segment_Display u_7_segment_display_1 (
    .g(seven_segment_circuit16_1_g), .f(seven_segment_circuit16_1_f), .a(seven_segment_circuit16_1_a),
    .b(seven_segment_circuit16_1_b), .e(seven_segment_circuit16_1_e), .d(seven_segment_circuit16_1_d),
    .c(seven_segment_circuit16_1_c));  // open: dp
  _7_Segment_Display u_7_segment_display_2 (
    .g(seven_segment_circuit16_2_g), .f(seven_segment_circuit16_2_f), .a(seven_segment_circuit16_2_a),
    .b(seven_segment_circuit16_2_b), .e(seven_segment_circuit16_2_e), .d(seven_segment_circuit16_2_d),
    .c(seven_segment_circuit16_2_c));  // open: dp
  adder_8 adder_8_1 (.A(adder_8_2_s), .B(register_8_2_o), .S(adder_8_1_s));  // open: Cout
  // Probe on adder_8_1_s
  adder_4 adder_4_1 (.A(4'b0001), .B(register_4_1_o), .Cout(adder_4_1_cout), .S(adder_4_1_s));
  adder_8 adder_8_2 (.A(8'h1), .B(register_8_1_o), .Cout(adder_8_2_cout), .S(adder_8_2_s));
  // Probe on adder_8_2_s
  Register_8 register_8_2 (.D(adder_8_1_s), .RE(in_8), .EN(in_9), .clk(button_10_out), .O(register_8_2_o));
  adder_4 adder_4_2 (.A(4'b0001), .B(register_4_2_o), .S(adder_4_2_s));  // open: Cout
  D_Flip_Flop_part d_ff_1 (.D(comparator_1_eq), .clk(clock_1_out), .Q(d_ff_1_q));  // open: Qn, preset, reset
  adder_4 adder_4_3 (.A(multiplexer_2_out), .B(register_4_3_o), .S(adder_4_3_s));  // open: Cout
  D_Flip_Flop_part d_ff_2 (.D(comparator_2_eq), .clk(clock_1_out), .Q(d_ff_2_q));  // open: Qn, preset, reset
  adder_4 adder_4_4 (.A(multiplexer_3_out), .B(register_4_4_o), .S(adder_4_4_s));  // open: Cout
  D_Flip_Flop_part d_ff_3 (.D(comparator_3_eq), .clk(clock_1_out), .Q(d_ff_3_q));  // open: Qn, preset, reset
  adder_4 adder_4_5 (.A(multiplexer_4_out), .B(register_4_5_o), .S(adder_4_5_s));  // open: Cout
  D_Flip_Flop_part d_ff_4 (.D(comparator_4_eq), .clk(clock_1_out), .Q(d_ff_4_q));  // open: Qn, preset, reset
  Comparator #(.width(4)) comparator_1 (.a(adder_4_2_s), .b(4'b1001), .eq(comparator_1_eq));  // open: gt, lt
  Comparator #(.width(4)) comparator_2 (.a(adder_4_3_s), .b(4'b0101), .eq(comparator_2_eq));  // open: gt, lt
  Comparator #(.width(4)) comparator_3 (.a(adder_4_4_s), .b(4'b1001), .eq(comparator_3_eq));  // open: gt, lt
  Comparator #(.width(4)) comparator_4 (.a(adder_4_5_s), .b(4'b0101), .eq(comparator_4_eq));  // open: gt, lt
  seven_segment_circuit16 seven_segment_circuit16_3 (
    .in_1(register_4_5_o), .a(seven_segment_circuit16_3_a), .b(seven_segment_circuit16_3_b),
    .c(seven_segment_circuit16_3_c), .d(seven_segment_circuit16_3_d), .e(seven_segment_circuit16_3_e),
    .f(seven_segment_circuit16_3_f), .g(seven_segment_circuit16_3_g));
  seven_segment_circuit16 seven_segment_circuit16_4 (
    .in_1(register_4_4_o), .a(seven_segment_circuit16_4_a), .b(seven_segment_circuit16_4_b),
    .c(seven_segment_circuit16_4_c), .d(seven_segment_circuit16_4_d), .e(seven_segment_circuit16_4_e),
    .f(seven_segment_circuit16_4_f), .g(seven_segment_circuit16_4_g));
  _7_Segment_Display u_7_segment_display_3 (
    .g(seven_segment_circuit16_3_g), .f(seven_segment_circuit16_3_f), .a(seven_segment_circuit16_3_a),
    .b(seven_segment_circuit16_3_b), .e(seven_segment_circuit16_3_e), .d(seven_segment_circuit16_3_d),
    .c(seven_segment_circuit16_3_c));  // open: dp
  _7_Segment_Display u_7_segment_display_4 (
    .g(seven_segment_circuit16_4_g), .f(seven_segment_circuit16_4_f), .a(seven_segment_circuit16_4_a),
    .b(seven_segment_circuit16_4_b), .e(seven_segment_circuit16_4_e), .d(seven_segment_circuit16_4_d),
    .c(seven_segment_circuit16_4_c));  // open: dp
  seven_segment_circuit16 seven_segment_circuit16_5 (
    .in_1(register_4_3_o), .a(seven_segment_circuit16_5_a), .b(seven_segment_circuit16_5_b),
    .c(seven_segment_circuit16_5_c), .d(seven_segment_circuit16_5_d), .e(seven_segment_circuit16_5_e),
    .f(seven_segment_circuit16_5_f), .g(seven_segment_circuit16_5_g));
  seven_segment_circuit16 seven_segment_circuit16_6 (
    .in_1(register_4_2_o), .a(seven_segment_circuit16_6_a), .b(seven_segment_circuit16_6_b),
    .c(seven_segment_circuit16_6_c), .d(seven_segment_circuit16_6_d), .e(seven_segment_circuit16_6_e),
    .f(seven_segment_circuit16_6_f), .g(seven_segment_circuit16_6_g));
  _7_Segment_Display u_7_segment_display_5 (
    .g(seven_segment_circuit16_5_g), .f(seven_segment_circuit16_5_f), .a(seven_segment_circuit16_5_a),
    .b(seven_segment_circuit16_5_b), .e(seven_segment_circuit16_5_e), .d(seven_segment_circuit16_5_d),
    .c(seven_segment_circuit16_5_c));  // open: dp
  _7_Segment_Display u_7_segment_display_6 (
    .g(seven_segment_circuit16_6_g), .f(seven_segment_circuit16_6_f), .a(seven_segment_circuit16_6_a),
    .b(seven_segment_circuit16_6_b), .e(seven_segment_circuit16_6_e), .d(seven_segment_circuit16_6_d),
    .c(seven_segment_circuit16_6_c));  // open: dp

  // Notes on the sheet:
  //   D锁存器
  //   D
  //   D触发器
  //   SR锁存器
  //   ~S~R锁存器
  //   R
  //   S
  //   WE
  //   带复位的D锁存器
  //   R
  //   D
  //   D锁存器实现位翻转功能
  //   R
  //   D
  //   带复位的D触发器
  //   D触发器实现位翻转
  //   下降沿D触发器
  //   带使能的D触发器
  //   WE
  //   WE
  //   带使能的D触发器2
  //   带复位的D触发器2(低电平置0，同步复位)
  //   4位寄存器
  //   clk
  //   Q
  //   4位计数器
  //   数字时钟
  //   秒1
  //   秒2
  //   分1
  //   分2
  //   数列求和
  //   A
  //   C
  //   B
  //   8位计数器
  //   D
endmodule

module SR_Latch (
  input  R,
  input  S,
  output Q,
  output NQ
);

  nor nor_1 (Q, R, NQ);
  nor nor_2 (NQ, Q, S);

  // Notes on the sheet:
  //   SR锁存器
endmodule

module D_Latch (
  input  WE,
  input  D,
  output Q,
  output NQ
);

  wire and_1_out, and_2_out, not_1_out;

  not not_1 (not_1_out, D);
  and and_1 (and_1_out, D, WE);
  and and_2 (and_2_out, WE, not_1_out);
  SR_Latch sr_latch_1 (.R(and_2_out), .S(and_1_out), .Q(Q), .NQ(NQ));

  // Notes on the sheet:
  //   D
  //   D锁存器
  //   WE
  //   Q
  //   ~Q
endmodule

module D_Flip_Flop (
  input  EN,
  input  clk,
  input  D,
  input  RE,
  output Q,
  output NQ
);

  wire and_1_out, d_latch_1_q, nor_1_out, not_1_out, not_2_out;

  not not_1 (not_1_out, D);
  and and_1 (and_1_out, EN, clk);
  not not_2 (not_2_out, clk);
  nor nor_1 (nor_1_out, not_1_out, RE);
  D_Latch d_latch_1 (.WE(not_2_out), .D(nor_1_out), .Q(d_latch_1_q));  // open: NQ
  D_Latch d_latch_2 (.WE(and_1_out), .D(d_latch_1_q), .Q(Q), .NQ(NQ));

  // Notes on the sheet:
  //   带使能的D触发器
endmodule

module Register_4 (
  input  [3:0] D,
  input  RE,
  input  EN,
  input  clk,
  output [3:0] O
);

  D_Flip_Flop d_flip_flop_1 (.EN(EN), .clk(clk), .D(D[0]), .RE(RE), .Q(O[0]));  // open: NQ
  D_Flip_Flop d_flip_flop_2 (.EN(EN), .clk(clk), .D(D[1]), .RE(RE), .Q(O[1]));  // open: NQ
  D_Flip_Flop d_flip_flop_3 (.EN(EN), .clk(clk), .D(D[2]), .RE(RE), .Q(O[2]));  // open: NQ
  D_Flip_Flop d_flip_flop_4 (.EN(EN), .clk(clk), .D(D[3]), .RE(RE), .Q(O[3]));  // open: NQ

  // Notes on the sheet:
  //   4位寄存器
endmodule

module Register_8 (
  input  [7:0] D,
  input  RE,
  input  EN,
  input  clk,
  output [7:0] O
);

  D_Flip_Flop d_flip_flop_1 (.EN(EN), .clk(clk), .D(D[0]), .RE(RE), .Q(O[0]));  // open: NQ
  D_Flip_Flop d_flip_flop_2 (.EN(EN), .clk(clk), .D(D[1]), .RE(RE), .Q(O[1]));  // open: NQ
  D_Flip_Flop d_flip_flop_3 (.EN(EN), .clk(clk), .D(D[2]), .RE(RE), .Q(O[2]));  // open: NQ
  D_Flip_Flop d_flip_flop_4 (.EN(EN), .clk(clk), .D(D[3]), .RE(RE), .Q(O[3]));  // open: NQ
  D_Flip_Flop d_flip_flop_5 (.EN(EN), .clk(clk), .D(D[4]), .RE(RE), .Q(O[4]));  // open: NQ
  D_Flip_Flop d_flip_flop_6 (.EN(EN), .clk(clk), .D(D[5]), .RE(RE), .Q(O[5]));  // open: NQ
  D_Flip_Flop d_flip_flop_7 (.EN(EN), .clk(clk), .D(D[6]), .RE(RE), .Q(O[6]));  // open: NQ
  D_Flip_Flop d_flip_flop_8 (.EN(EN), .clk(clk), .D(D[7]), .RE(RE), .Q(O[7]));  // open: NQ

  // Notes on the sheet:
  //   8位寄存器
endmodule

module adder_8 (
  input  [7:0] A,
  input  [7:0] B,
  output Cout,
  output [7:0] S
);

  wire full_adder_1_cout, full_adder_2_cout, full_adder_3_cout, full_adder_4_cout, full_adder_5_cout,
       full_adder_6_cout, half_adder_1_c;

  Half_adder half_adder_1 (.in_1(A[0]), .in_2(B[0]), .S(S[0]), .C(half_adder_1_c));
  Full_Adder full_adder_1 (.Cin(half_adder_1_c), .A(A[1]), .B(B[1]), .Cout(full_adder_1_cout), .S(S[1]));
  Full_Adder full_adder_2 (.Cin(full_adder_1_cout), .A(A[2]), .B(B[2]), .Cout(full_adder_2_cout), .S(S[2]));
  Full_Adder full_adder_3 (.Cin(full_adder_2_cout), .A(A[3]), .B(B[3]), .Cout(full_adder_3_cout), .S(S[3]));
  Full_Adder full_adder_4 (.Cin(full_adder_3_cout), .A(A[4]), .B(B[4]), .Cout(full_adder_4_cout), .S(S[4]));
  Full_Adder full_adder_5 (.Cin(full_adder_4_cout), .A(A[5]), .B(B[5]), .Cout(full_adder_5_cout), .S(S[5]));
  Full_Adder full_adder_6 (.Cin(full_adder_5_cout), .A(A[6]), .B(B[6]), .Cout(full_adder_6_cout), .S(S[6]));
  Full_Adder full_adder_7 (.Cin(full_adder_6_cout), .A(A[7]), .B(B[7]), .Cout(Cout), .S(S[7]));
endmodule

module ttt (
  input  in_1,
  input  in_2,
  input  in_3,
  input  in_4
);

  wire clock_1_out, comparator_1_eq, comparator_2_eq, d_ff_1_q, or_1_out, or_2_out,
       seven_segment_circuit16_1_a, seven_segment_circuit16_1_b, seven_segment_circuit16_1_c,
       seven_segment_circuit16_1_d, seven_segment_circuit16_1_e, seven_segment_circuit16_1_f,
       seven_segment_circuit16_1_g, seven_segment_circuit16_2_a, seven_segment_circuit16_2_b,
       seven_segment_circuit16_2_c, seven_segment_circuit16_2_d, seven_segment_circuit16_2_e,
       seven_segment_circuit16_2_f, seven_segment_circuit16_2_g, seven_segment_circuit16_3_a,
       seven_segment_circuit16_3_b, seven_segment_circuit16_3_c, seven_segment_circuit16_3_d,
       seven_segment_circuit16_3_e, seven_segment_circuit16_3_f, seven_segment_circuit16_3_g,
       seven_segment_circuit16_4_a, seven_segment_circuit16_4_b, seven_segment_circuit16_4_c,
       seven_segment_circuit16_4_d, seven_segment_circuit16_4_e, seven_segment_circuit16_4_f,
       seven_segment_circuit16_4_g;
  wire [7:0] adder_8_1_s, adder_8_2_s, multiplexer_1_out, register_8_1_o, register_8_2_o;

  or or_1 (or_1_out, in_3, comparator_2_eq);
  or or_2 (or_2_out, in_1, d_ff_1_q);
  Clock clock_1 (.out(clock_1_out));
  Register_8 register_8_1 (.D(adder_8_1_s), .RE(or_2_out), .EN(in_2), .clk(clock_1_out), .O(register_8_1_o));
  Register_8 register_8_2 (.D(adder_8_2_s), .RE(or_1_out), .EN(in_4), .clk(clock_1_out), .O(register_8_2_o));
  Multiplexer #(.width(8)) multiplexer_1 (.in0({8{1'b0}}), .in1(8'h1), .out(multiplexer_1_out), .sel(d_ff_1_q));
  D_Flip_Flop_part d_ff_1 (.D(comparator_1_eq), .clk(clock_1_out), .Q(d_ff_1_q));  // open: Qn, preset, reset
  adder_8 adder_8_1 (.A(8'h1), .B(register_8_1_o), .S(adder_8_1_s));  // open: Cout
  adder_8 adder_8_2 (.A(multiplexer_1_out), .B(register_8_2_o), .S(adder_8_2_s));  // open: Cout
  Comparator comparator_1 (.a(adder_8_1_s), .b(8'h3b), .eq(comparator_1_eq));  // open: gt, lt
  Comparator comparator_2 (.a(adder_8_2_s), .b(8'h3b), .eq(comparator_2_eq));  // open: gt, lt
  seven_segment_circuit16 seven_segment_circuit16_1 (
    .in_1(register_8_2_o[7:4]), .a(seven_segment_circuit16_1_a), .b(seven_segment_circuit16_1_b),
    .c(seven_segment_circuit16_1_c), .d(seven_segment_circuit16_1_d), .e(seven_segment_circuit16_1_e),
    .f(seven_segment_circuit16_1_f), .g(seven_segment_circuit16_1_g));
  seven_segment_circuit16 seven_segment_circuit16_2 (
    .in_1(register_8_2_o[3:0]), .a(seven_segment_circuit16_2_a), .b(seven_segment_circuit16_2_b),
    .c(seven_segment_circuit16_2_c), .d(seven_segment_circuit16_2_d), .e(seven_segment_circuit16_2_e),
    .f(seven_segment_circuit16_2_f), .g(seven_segment_circuit16_2_g));
  _7_Segment_Display u_7_segment_display_1 (
    .g(seven_segment_circuit16_1_g), .f(seven_segment_circuit16_1_f), .a(seven_segment_circuit16_1_a),
    .b(seven_segment_circuit16_1_b), .e(seven_segment_circuit16_1_e), .d(seven_segment_circuit16_1_d),
    .c(seven_segment_circuit16_1_c));  // open: dp
  _7_Segment_Display u_7_segment_display_2 (
    .g(seven_segment_circuit16_2_g), .f(seven_segment_circuit16_2_f), .a(seven_segment_circuit16_2_a),
    .b(seven_segment_circuit16_2_b), .e(seven_segment_circuit16_2_e), .d(seven_segment_circuit16_2_d),
    .c(seven_segment_circuit16_2_c));  // open: dp
  seven_segment_circuit16 seven_segment_circuit16_3 (
    .in_1(register_8_1_o[7:4]), .a(seven_segment_circuit16_3_a), .b(seven_segment_circuit16_3_b),
    .c(seven_segment_circuit16_3_c), .d(seven_segment_circuit16_3_d), .e(seven_segment_circuit16_3_e),
    .f(seven_segment_circuit16_3_f), .g(seven_segment_circuit16_3_g));
  seven_segment_circuit16 seven_segment_circuit16_4 (
    .in_1(register_8_1_o[3:0]), .a(seven_segment_circuit16_4_a), .b(seven_segment_circuit16_4_b),
    .c(seven_segment_circuit16_4_c), .d(seven_segment_circuit16_4_d), .e(seven_segment_circuit16_4_e),
    .f(seven_segment_circuit16_4_f), .g(seven_segment_circuit16_4_g));
  _7_Segment_Display u_7_segment_display_3 (
    .g(seven_segment_circuit16_3_g), .f(seven_segment_circuit16_3_f), .a(seven_segment_circuit16_3_a),
    .b(seven_segment_circuit16_3_b), .e(seven_segment_circuit16_3_e), .d(seven_segment_circuit16_3_d),
    .c(seven_segment_circuit16_3_c));  // open: dp
  _7_Segment_Display u_7_segment_display_4 (
    .g(seven_segment_circuit16_4_g), .f(seven_segment_circuit16_4_f), .a(seven_segment_circuit16_4_a),
    .b(seven_segment_circuit16_4_b), .e(seven_segment_circuit16_4_e), .d(seven_segment_circuit16_4_d),
    .c(seven_segment_circuit16_4_c));  // open: dp

  // Notes on the sheet:
  //   数字时钟
  //   秒
  //   分
endmodule
