// Logisim project sCPU.circ as structural Verilog: 10 circuits, main circuit main
module main (
  input  [2:0] in_1,
  input  [1:0] in_2,
  input  [7:0] in_3,
  input  in_4,
  input  in_5,
  input  [1:0] in_6,
  input  in_7,
  input  [7:0] in_8,
  input  in_9,
  input  in_10,
  input  in_11,
  input  in_12,
  input  in_13,
  output [7:0] out_14,
  output [7:0] out_15,
  output [7:0] out_16
);

  wire and_1_out, and_2_out, and_3_out, button_1_out, button_2_out, button_3_out, button_4_out, button_5_out,
       clock_1_out, decoder_1_out0, decoder_1_out1, decoder_1_out2, decoder_1_out3, decoder_2_out0,
       decoder_2_out2, decoder_3_out0, decoder_3_out2, decoder_3_out3, decoder_4_out0, decoder_4_out2,
       decoder_4_out3, decoder_5_out0, decoder_5_out1, decoder_5_out2, decoder_5_out3, decoder_6_out0,
       decoder_6_out1, decoder_6_out2, decoder_6_out3, my_bner0_1_equal, my_bner0_2_equal, my_bner0_3_equal,
       not_1_out, not_2_out, not_3_out, or_1_out, or_2_out, or_3_out, or_4_out, seven_segment_circuit16_1_a,
       seven_segment_circuit16_1_b, seven_segment_circuit16_1_c, seven_segment_circuit16_1_d,
       seven_segment_circuit16_1_e, seven_segment_circuit16_1_f, seven_segment_circuit16_1_g,
       seven_segment_circuit16_2_a, seven_segment_circuit16_2_b, seven_segment_circuit16_2_c,
       seven_segment_circuit16_2_d, seven_segment_circuit16_2_e, seven_segment_circuit16_2_f,
       seven_segment_circuit16_2_g, undriven, undriven_2, undriven_3, undriven_4;
  wire [1:0] multiplexer_7_out, multiplexer_8_out, multiplexer_10_out, multiplexer_12_out,
       multiplexer_13_out, multiplexer_14_out, multiplexer_15_out, multiplexer_18_out, multiplexer_19_out,
       multiplexer_20_out, my_add_1_rd, my_add_1_rs1, my_add_1_rs2, my_add_2_rd, my_add_2_rs1, my_add_2_rs2,
       my_add_3_rd, my_add_3_rs1, my_add_3_rs2, my_add_4_rd, my_add_4_rs1, my_add_4_rs2, my_bner0_1_r0,
       my_bner0_1_rs2, my_bner0_2_r0, my_bner0_2_rs2, my_bner0_3_r0, my_bner0_3_rs2, my_li_1_add_r,
       my_li_2_add_r, my_li_3_add_r, my_li_4_add_r, my_out_1_rs, my_sum_1_10_all_1_q, my_sum_1_10_all_2_q,
       my_sum_1_10_odd_1_q;
  wire [3:0] adder_1_out, adder_2_out, adder_3_out, adder_4_out, adder_5_out, multiplexer_2_out,
       multiplexer_3_out, multiplexer_16_out, my_bner0_1_addr, my_bner0_2_addr, my_bner0_3_addr,
       register_1_q, register_2_q, register_3_q, register_4_q, register_13_q;
  wire [5:0] my_sum_1_10_all_1_q_2, my_sum_1_10_all_2_q_2, my_sum_1_10_odd_1_q_2;
  wire [7:0] and_4_out, bit_extender_1_out, multiplexer_6_out, multiplexer_9_out, multiplexer_11_out,
       multiplexer_17_out, my_add_1_wdata, my_add_2_wdata, my_add_3_wdata, my_add_4_wdata, my_gpr2_1_rdata1,
       my_gpr2_1_rdata2, my_gpr2_2_rdata1, my_gpr2_2_rdata2, my_gpr2_3_rdata1, my_gpr2_3_rdata2,
       my_gpr2_4_rdata1, my_gpr2_4_rdata2, my_gpr_1_q, my_li_1_d, my_li_2_d, my_li_3_d, my_li_4_d,
       my_sum_1_10_all_3_q, my_sum_1_10_all_with_out_1_q, register_5_q, register_6_q, register_7_q,
       register_8_q, register_9_q, register_10_q, register_11_q, register_12_q;

  Button button_1 (.out(button_1_out));
  Register #(.width(4)) register_1 (.D(adder_1_out), .en(in_11), .clk(button_2_out), .Q(register_1_q));  // open: clr
  Button button_2 (.out(button_2_out));
  Register #(.width(4)) register_2 (
    .D(multiplexer_2_out), .en(in_12), .clk(button_1_out), .Q(register_2_q));  // open: clr
  Register #(.width(4)) register_3 (
    .D(multiplexer_3_out), .en(in_13), .clk(button_3_out), .Q(register_3_q));  // open: clr
  Button button_3 (.out(button_3_out));
  Multiplexer #(.select(3), .width(8)) multiplexer_1 (
    .in0(8'h8a), .in1(8'h90), .in2(8'ha0), .in3(8'hb1), .in4(8'h17), .in5(8'h29), .in6(8'hd1), .in7(8'hdf),
    .out(out_14), .sel(in_1));
  Decoder #(.select(2)) decoder_1 (
    .out0(decoder_1_out0), .out1(decoder_1_out1), .out2(decoder_1_out2), .out3(decoder_1_out3), .sel(in_6),
    .en(in_9));
  Button button_4 (.out(button_4_out));
  Clock clock_1 (.out(clock_1_out));
  Register #(.width(4)) register_4 (.D(adder_4_out), .en(in_10), .clk(button_4_out), .Q(register_4_q));  // open: clr
  Adder #(.width(4)) adder_1 (.a(4'b0001), .b(register_1_q), .out(adder_1_out));  // open: cin, cout
  Adder #(.width(4)) adder_2 (.a(4'b0001), .b(register_2_q), .out(adder_2_out));  // open: cin, cout
  Adder #(.width(4)) adder_3 (.a(4'b0001), .b(register_3_q), .out(adder_3_out));  // open: cin, cout
  Register register_5 (.D(in_8), .en(decoder_1_out0), .clk(clock_1_out), .Q(register_5_q));  // open: clr
  Register register_6 (.D(in_8), .en(decoder_1_out1), .clk(clock_1_out), .Q(register_6_q));  // open: clr
  Register register_7 (.D(in_8), .en(decoder_1_out2), .clk(clock_1_out), .Q(register_7_q));  // open: clr
  Register register_8 (.D(in_8), .en(decoder_1_out3), .clk(clock_1_out), .Q(register_8_q));  // open: clr
  Adder #(.width(4)) adder_4 (.a(4'b0001), .b(register_4_q), .out(adder_4_out));  // open: cin, cout
  Multiplexer #(.width(4)) multiplexer_2 (
    .in0(adder_2_out), .in1(my_bner0_1_addr), .out(multiplexer_2_out), .sel(and_1_out));
  Multiplexer #(.width(4)) multiplexer_3 (
    .in0(adder_3_out), .in1(my_bner0_2_addr), .out(multiplexer_3_out), .sel(and_2_out));
  Multiplexer #(.select(2), .width(8)) multiplexer_4 (
    .in0(register_5_q), .in1(register_6_q), .in2(register_7_q), .in3(register_8_q), .out(out_16), .sel(in_6));
  my_sum_1_10_all my_sum_1_10_all_1 (.addr(register_1_q), .Q({my_sum_1_10_all_1_q, my_sum_1_10_all_1_q_2}));
  my_sum_1_10_all my_sum_1_10_all_2 (.addr(register_2_q), .Q({my_sum_1_10_all_2_q, my_sum_1_10_all_2_q_2}));
  my_sum_1_10_odd my_sum_1_10_odd_1 (.addr(register_3_q), .Q({my_sum_1_10_odd_1_q, my_sum_1_10_odd_1_q_2}));
  my_sum_1_10_all my_sum_1_10_all_3 (.addr(register_4_q), .Q(my_sum_1_10_all_3_q));
  not not_1 (not_1_out, my_bner0_1_equal);
  and and_1 (and_1_out, not_1_out, decoder_3_out3);
  not not_2 (not_2_out, my_bner0_2_equal);
  and and_2 (and_2_out, not_2_out, decoder_4_out3);
  Decoder #(.select(2)) decoder_2 (
    .out0(decoder_2_out0), .out2(decoder_2_out2), .sel(my_sum_1_10_all_1_q), .en(undriven_2));  // open: out1, out3
  Decoder #(.select(2)) decoder_3 (
    .out0(decoder_3_out0), .out2(decoder_3_out2), .out3(decoder_3_out3), .sel(my_sum_1_10_all_2_q),
    .en(undriven));  // open: out1
  Decoder #(.select(2)) decoder_4 (
    .out0(decoder_4_out0), .out2(decoder_4_out2), .out3(decoder_4_out3), .sel(my_sum_1_10_odd_1_q),
    .en(undriven_3));  // open: out1
  Decoder #(.select(2)) decoder_5 (
    .out0(decoder_5_out0), .out1(decoder_5_out1), .out2(decoder_5_out2), .out3(decoder_5_out3), .sel(in_2),
    .en(in_4));
  // Probe on my_gpr_1_q
  my_GPR my_gpr_1 (
    .addr(my_sum_1_10_all_3_q[5:4]), .D({4'b0000, my_sum_1_10_all_3_q[3:0]}), .EN(in_10), .clk(button_4_out),
    .Q(my_gpr_1_q));
  Register register_9 (.D(in_3), .en(decoder_5_out0), .clk(in_5), .Q(register_9_q));  // open: clr
  Register register_10 (.D(in_3), .en(decoder_5_out1), .clk(in_5), .Q(register_10_q));  // open: clr
  Register register_11 (.D(in_3), .en(decoder_5_out2), .clk(in_5), .Q(register_11_q));  // open: clr
  Register register_12 (.D(in_3), .en(decoder_5_out3), .clk(in_5), .Q(register_12_q));  // open: clr
  my_li my_li_1 (.I({my_sum_1_10_all_1_q, my_sum_1_10_all_1_q_2}), .D(my_li_1_d), .add_R(my_li_1_add_r));
  my_add my_add_1 (
    .I({my_sum_1_10_all_1_q, my_sum_1_10_all_1_q_2}), .rdata1(my_gpr2_1_rdata1), .rdata2(my_gpr2_1_rdata2),
    .rs2(my_add_1_rs2), .rs1(my_add_1_rs1), .rd(my_add_1_rd), .wdata(my_add_1_wdata));
  my_bner0 my_bner0_1 (
    .I({my_sum_1_10_all_2_q, my_sum_1_10_all_2_q_2}), .r0data(my_gpr2_2_rdata1), .rs2data(my_gpr2_2_rdata2),
    .r0(my_bner0_1_r0), .rs2(my_bner0_1_rs2), .addr(my_bner0_1_addr), .equal(my_bner0_1_equal));
  my_li my_li_2 (.I({my_sum_1_10_all_2_q, my_sum_1_10_all_2_q_2}), .D(my_li_2_d), .add_R(my_li_2_add_r));
  my_add my_add_2 (
    .I({my_sum_1_10_all_2_q, my_sum_1_10_all_2_q_2}), .rdata1(my_gpr2_2_rdata1), .rdata2(my_gpr2_2_rdata2),
    .rs2(my_add_2_rs2), .rs1(my_add_2_rs1), .rd(my_add_2_rd), .wdata(my_add_2_wdata));
  my_bner0 my_bner0_2 (
    .I({my_sum_1_10_odd_1_q, my_sum_1_10_odd_1_q_2}), .r0data(my_gpr2_3_rdata1), .rs2data(my_gpr2_3_rdata2),
    .r0(my_bner0_2_r0), .rs2(my_bner0_2_rs2), .addr(my_bner0_2_addr), .equal(my_bner0_2_equal));
  my_li my_li_3 (.I({my_sum_1_10_odd_1_q, my_sum_1_10_odd_1_q_2}), .D(my_li_3_d), .add_R(my_li_3_add_r));
  my_add my_add_3 (
    .I({my_sum_1_10_odd_1_q, my_sum_1_10_odd_1_q_2}), .rdata1(my_gpr2_3_rdata1), .rdata2(my_gpr2_3_rdata2),
    .rs2(my_add_3_rs2), .rs1(my_add_3_rs1), .rd(my_add_3_rd), .wdata(my_add_3_wdata));
  Multiplexer #(.select(2), .width(8)) multiplexer_5 (
    .in0(register_9_q), .in1(register_10_q), .in2(register_11_q), .in3(register_12_q), .out(out_15),
    .sel(in_2));
  Multiplexer #(.width(8)) multiplexer_6 (
    .in0(my_li_1_d), .in1(my_add_1_wdata), .out(multiplexer_6_out), .sel(decoder_2_out0));
  Multiplexer #(.width(2)) multiplexer_7 (
    .in0(my_li_1_add_r), .in1(my_add_1_rd), .out(multiplexer_7_out), .sel(decoder_2_out0));
  Multiplexer #(.width(2)) multiplexer_8 (
    .in0(my_add_2_rs1), .in1(my_bner0_1_r0), .out(multiplexer_8_out), .sel(decoder_3_out3));
  Multiplexer #(.width(8)) multiplexer_9 (
    .in0(my_li_2_d), .in1(my_add_2_wdata), .out(multiplexer_9_out), .sel(decoder_3_out0));
  Multiplexer #(.width(2)) multiplexer_10 (
    .in0(my_li_2_add_r), .in1(my_add_2_rd), .out(multiplexer_10_out), .sel(decoder_3_out0));
  Multiplexer #(.width(8)) multiplexer_11 (
    .in0(my_li_3_d), .in1(my_add_3_wdata), .out(multiplexer_11_out), .sel(decoder_4_out0));
  Multiplexer #(.width(2)) multiplexer_12 (
    .in0(my_li_3_add_r), .in1(my_add_3_rd), .out(multiplexer_12_out), .sel(decoder_4_out0));
  or or_1 (or_1_out, decoder_2_out0, decoder_2_out2);
  Multiplexer #(.width(2)) multiplexer_13 (
    .in0(my_add_2_rs2), .in1(my_bner0_1_rs2), .out(multiplexer_13_out), .sel(decoder_3_out3));
  or or_2 (or_2_out, decoder_3_out0, decoder_3_out2);
  Multiplexer #(.width(2)) multiplexer_14 (
    .in0(my_add_3_rs1), .in1(my_bner0_2_r0), .out(multiplexer_14_out), .sel(decoder_4_out3));
  Multiplexer #(.width(2)) multiplexer_15 (
    .in0(my_add_3_rs2), .in1(my_bner0_2_rs2), .out(multiplexer_15_out), .sel(decoder_4_out3));
  or or_3 (or_3_out, decoder_4_out0, decoder_4_out2);
  my_GPR2 my_gpr2_1 (
    .raddr1(my_add_1_rs1), .raddr2(my_add_1_rs2), .wdata(multiplexer_6_out), .wen(or_1_out),
    .clk(button_2_out), .waddr(multiplexer_7_out), .rdata1(my_gpr2_1_rdata1), .rdata2(my_gpr2_1_rdata2));
  my_GPR2 my_gpr2_2 (
    .raddr1(multiplexer_8_out), .raddr2(multiplexer_13_out), .wdata(multiplexer_9_out), .wen(or_2_out),
    .clk(button_1_out), .waddr(multiplexer_10_out), .rdata1(my_gpr2_2_rdata1), .rdata2(my_gpr2_2_rdata2));
  my_GPR2 my_gpr2_3 (
    .raddr1(multiplexer_14_out), .raddr2(multiplexer_15_out), .wdata(multiplexer_11_out), .wen(or_3_out),
    .clk(button_3_out), .waddr(multiplexer_12_out), .rdata1(my_gpr2_3_rdata1), .rdata2(my_gpr2_3_rdata2));
  Register #(.width(4)) register_13 (
    .D(multiplexer_16_out), .en(in_7), .clk(button_5_out), .Q(register_13_q));  // open: clr
  Button button_5 (.out(button_5_out));
  Adder #(.width(4)) adder_5 (.a(4'b0001), .b(register_13_q), .out(adder_5_out));  // open: cin, cout
  Multiplexer #(.width(4)) multiplexer_16 (
    .in0(adder_5_out), .in1(my_bner0_3_addr), .out(multiplexer_16_out), .sel(and_3_out));
  my_sum_1_10_all_with_out my_sum_1_10_all_with_out_1 (.addr(register_13_q), .Q(my_sum_1_10_all_with_out_1_q));
  not not_3 (not_3_out, my_bner0_3_equal);
  and and_3 (and_3_out, not_3_out, decoder_6_out3);
  Decoder #(.select(2)) decoder_6 (
    .out0(decoder_6_out0), .out1(decoder_6_out1), .out2(decoder_6_out2), .out3(decoder_6_out3),
    .sel(my_sum_1_10_all_with_out_1_q[7:6]), .en(undriven_4));
  my_out my_out_1 (.I(my_sum_1_10_all_with_out_1_q), .rs(my_out_1_rs));
  my_bner0 my_bner0_3 (
    .I(my_sum_1_10_all_with_out_1_q), .r0data(my_gpr2_4_rdata1), .rs2data(my_gpr2_4_rdata2),
    .r0(my_bner0_3_r0), .rs2(my_bner0_3_rs2), .addr(my_bner0_3_addr), .equal(my_bner0_3_equal));
  my_li my_li_4 (.I(my_sum_1_10_all_with_out_1_q), .D(my_li_4_d), .add_R(my_li_4_add_r));
  my_add my_add_4 (
    .I(my_sum_1_10_all_with_out_1_q), .rdata1(my_gpr2_4_rdata1), .rdata2(my_gpr2_4_rdata2),
    .rs2(my_add_4_rs2), .rs1(my_add_4_rs1), .rd(my_add_4_rd), .wdata(my_add_4_wdata));
  Multiplexer #(.select(2), .width(8)) multiplexer_17 (
    .in0(my_add_4_wdata), .in2(my_li_4_d), .out(multiplexer_17_out), .sel(my_sum_1_10_all_with_out_1_q[7:6]));  // open: in1, in3
  Multiplexer #(.select(2), .width(2)) multiplexer_18 (
    .in0(my_add_4_rd), .in2(my_li_4_add_r), .out(multiplexer_18_out), .sel(my_sum_1_10_all_with_out_1_q[7:6]));  // open: in1, in3
  Multiplexer #(.select(2), .width(2)) multiplexer_19 (
    .in0(my_add_4_rs1), .in1(my_out_1_rs), .in3(my_bner0_3_r0), .out(multiplexer_19_out),
    .sel(my_sum_1_10_all_with_out_1_q[7:6]));  // open: in2
  Multiplexer #(.select(2), .width(2)) multiplexer_20 (
    .in0(my_add_4_rs2), .in3(my_bner0_3_rs2), .out(multiplexer_20_out),
    .sel(my_sum_1_10_all_with_out_1_q[7:6]));  // open: in1, in2
  or or_4 (or_4_out, decoder_6_out0, decoder_6_out2);
  my_GPR2 my_gpr2_4 (
    .raddr1(multiplexer_19_out), .raddr2(multiplexer_20_out), .wdata(multiplexer_17_out), .wen(or_4_out),
    .clk(button_5_out), .waddr(multiplexer_18_out), .rdata1(my_gpr2_4_rdata1), .rdata2(my_gpr2_4_rdata2));
  assign bit_extender_1_out = {{7{decoder_6_out1}}, decoder_6_out1};  // Bit_Extender bit_extender_1
  assign and_4_out = bit_extender_1_out & my_gpr2_4_rdata1;  // AND_Gate and_4, 8 bits wide
  seven_segment_circuit16 seven_segment_circuit16_1 (
    .in_1(and_4_out[7:4]), .a(seven_segment_circuit16_1_a), .b(seven_segment_circuit16_1_b),
    .c(seven_segment_circuit16_1_c), .d(seven_segment_circuit16_1_d), .e(seven_segment_circuit16_1_e),
    .f(seven_segment_circuit16_1_f), .g(seven_segment_circuit16_1_g));
  seven_segment_circuit16 seven_segment_circuit16_2 (
    .in_1(and_4_out[3:0]), .a(seven_segment_circuit16_2_a), .b(seven_segment_circuit16_2_b),
    .c(seven_segment_circuit16_2_c), .d(seven_segment_circuit16_2_d), .e(seven_segment_circuit16_2_e),
    .f(seven_segment_circuit16_2_f), .g(seven_segment_circuit16_2_g));
  _7_Segment_Display u_7_segment_display_1 (
    .g(seven_segment_circuit16_1_g), .f(seven_segment_circuit16_1_f), .a(seven_segment_circuit16_1_a),
    .b(seven_segment_circuit16_1_b), .e(seven_segment_circuit16_1_e), .d(seven_segment_circuit16_1_d),
    .c(seven_segment_circuit16_1_c));  // open: dp
  _7_Segment_Display u_7_segment_display_2 (
    .g(seven_segment_circuit16_2_g), .f(seven_segment_circuit16_2_f), .a(seven_segment_circuit16_2_a),
    .b(seven_segment_circuit16_2_b), .e(seven_segment_circuit16_2_e), .d(seven_segment_circuit16_2_d),
    .c(seven_segment_circuit16_2_c));  // open: dp

  // Notes on the sheet:
  //   RAM
  //   实现li和add指令的sCPU
  //   实现li和add指令的sCPU
  //   实现li,add和bner0指令的sCPU
  //   多路选择器实现数列求和的指令ROM
  //   实现li指令的sCPU
  //   取指
  //   取指
  //   取指
  //   取指
  //   译码
  //   译码
  //   译码
  //   译码先跳过
  //   执行
  //   GPR
  //   实现li，add，bner0和out指令的sCPU
  //   取指
  //   译码
endmodule

module my_sum_1_10_all (
  input  [3:0] addr,
  output [7:0] Q
);

  Multiplexer #(.select(4), .width(8)) multiplexer_1 (
    .in0(8'h8a), .in1(8'h90), .in2(8'ha0), .in3(8'hb1), .in4(8'h17), .in5(8'h29), .in6(8'hd1), .in7(8'hdf),
    .out(Q), .sel(addr));  // open: in8, in9, in10, in11, in12, in13, in14, in15

  // Notes on the sheet:
  //   多路选择器实现数列求和的指令ROM
endmodule

module my_GPR (
  input  [1:0] addr,
  input  [7:0] D,
  input  EN,
  input  clk,
  output [7:0] Q
);

  wire decoder_1_out0, decoder_1_out1, decoder_1_out2, decoder_1_out3;
  wire [7:0] register_1_q, register_2_q, register_3_q, register_4_q;

  Decoder #(.select(2)) decoder_1 (
    .out0(decoder_1_out0), .out1(decoder_1_out1), .out2(decoder_1_out2), .out3(decoder_1_out3), .sel(addr),
    .en(EN));
  Register register_1 (.D(D), .en(decoder_1_out0), .clk(clk), .Q(register_1_q));  // open: clr
  Register register_2 (.D(D), .en(decoder_1_out1), .clk(clk), .Q(register_2_q));  // open: clr
  Register register_3 (.D(D), .en(decoder_1_out2), .clk(clk), .Q(register_3_q));  // open: clr
  Register register_4 (.D(D), .en(decoder_1_out3), .clk(clk), .Q(register_4_q));  // open: clr
  Multiplexer #(.select(2), .width(8)) multiplexer_1 (
    .in0(register_1_q), .in1(register_2_q), .in2(register_3_q), .in3(register_4_q), .out(Q), .sel(addr));

  // Notes on the sheet:
  //   GPR
endmodule

module my_li (
  input  [7:0] I,
  output [7:0] D,
  output [1:0] add_R
);


  assign add_R = I[5:4];
  assign D = {4'b0000, I[3:0]};

  // Notes on the sheet:
  //   译码、执行部分
endmodule

module my_GPR2 (
  input  [1:0] raddr1,
  input  [1:0] raddr2,
  input  [7:0] wdata,
  input  wen,
  input  clk,
  input  [1:0] waddr,
  output [7:0] rdata1,
  output [7:0] rdata2
);

  wire decoder_1_out0, decoder_1_out1, decoder_1_out2, decoder_1_out3;
  wire [7:0] register_1_q, register_2_q, register_3_q, register_4_q;

  Decoder #(.select(2)) decoder_1 (
    .out0(decoder_1_out0), .out1(decoder_1_out1), .out2(decoder_1_out2), .out3(decoder_1_out3), .sel(waddr),
    .en(wen));
  Register register_1 (.D(wdata), .en(decoder_1_out0), .clk(clk), .Q(register_1_q));  // open: clr
  Register register_2 (.D(wdata), .en(decoder_1_out1), .clk(clk), .Q(register_2_q));  // open: clr
  Register register_3 (.D(wdata), .en(decoder_1_out2), .clk(clk), .Q(register_3_q));  // open: clr
  Register register_4 (.D(wdata), .en(decoder_1_out3), .clk(clk), .Q(register_4_q));  // open: clr
  Multiplexer #(.select(2), .width(8)) multiplexer_1 (
    .in0(register_1_q), .in1(register_2_q), .in2(register_3_q), .in3(register_4_q), .out(rdata1), .sel(raddr1));
  Multiplexer #(.select(2), .width(8)) multiplexer_2 (
    .in0(register_1_q), .in1(register_2_q), .in2(register_3_q), .in3(register_4_q), .out(rdata2), .sel(raddr2));

  // Notes on the sheet:
  //   GPR2
endmodule

module my_add (
  input  [7:0] I,
  input  [7:0] rdata1,
  input  [7:0] rdata2,
  output [1:0] rs2,
  output [1:0] rs1,
  output [1:0] rd,
  output [7:0] wdata
);

  Adder adder_1 (.a(rdata1), .b(rdata2), .out(wdata));  // open: cin, cout

  assign rd = I[5:4];
  assign rs1 = I[3:2];
  assign rs2 = I[1:0];

  // Notes on the sheet:
  //   获取操作数
  //   执行部分
endmodule

module my_bner0 (
  input  [7:0] I,
  input  [7:0] r0data,
  input  [7:0] rs2data,
  output [1:0] r0,
  output [1:0] rs2,
  output [3:0] addr,
  output equal
);

  Comparator comparator_1 (.a(r0data), .b(rs2data), .eq(equal));  // open: gt, lt

  assign addr = I[5:2];
  assign r0 = 2'b00;
  assign rs2 = I[1:0];

  // Notes on the sheet:
  //   获取操作数
  //   执行部分
endmodule

module my_sum_1_10_odd (
  input  [3:0] addr,
  output [7:0] Q
);

  Multiplexer #(.select(4), .width(8)) multiplexer_1 (
    .in0(8'h89), .in1(8'h91), .in2(8'ha1), .in3(8'hb2), .in4(8'h17), .in5(8'h29), .in6(8'hd1), .in7(8'hdf),
    .out(Q), .sel(addr));  // open: in8, in9, in10, in11, in12, in13, in14, in15

  // Notes on the sheet:
  //   多路选择器实现数列求和的指令ROM
endmodule

module my_out (
  input  [7:0] I,
  output [1:0] rs
);


  assign rs = I[5:4];

  // Notes on the sheet:
  //   获取操作数
endmodule

module my_sum_1_10_all_with_out (
  input  [3:0] addr,
  output [7:0] Q
);

  Multiplexer #(.select(4), .width(8)) multiplexer_1 (
    .in0(8'h8a), .in1(8'h90), .in2(8'ha0), .in3(8'hb1), .in4(8'h17), .in5(8'h29), .in6(8'hd1), .in7(8'h60),
    .in8(8'hdf), .out(Q), .sel(addr));  // open: in9, in10, in11, in12, in13, in14, in15
endmodule
