// Logisim project minirv.circ as structural Verilog: 17 circuits, main circuit main
module main (
  input  in_1
);

  wire addiop, addop, and_1_out, and_2_out, and_3_out, and_4_out, clk, comparator_1_eq, comparator_2_eq,
       comparator_3_eq, comparator_4_eq, comparator_5_eq, comparator_6_eq, comparator_7_eq, comparator_8_eq,
       comparator_10_eq, comparator_11_eq, comparator_12_eq, comparator_13_eq, comparator_14_eq,
       comparator_15_eq, comparator_16_eq, demultiplexer_1_out0, demultiplexer_1_out1, demultiplexer_1_out2,
       demultiplexer_1_out3, jalrop, lbuop, luiop, lwop, ram_BE0, ram_BE1, ram_BE2, ram_BE3, ram_OE, ram_WE,
       sbop, swop, wen;
  wire [1:0] sb_ram_byte;
  wire [2:0] priority_encoder_1_out, priority_encoder_2_out, priority_encoder_3_out, rom_sum_1_out_2_3;
  wire [4:0] add_rd, add_rs1, add_rs2, addi_rd, addi_rs1, and_24_out, and_25_out, and_26_out, and_27_out,
       and_28_out, and_29_out, and_30_out, and_31_out, and_32_out, and_33_out, and_34_out, and_35_out,
       and_36_out, and_37_out, and_38_out, and_39_out, bit_extender_13_out, bit_extender_14_out,
       bit_extender_15_out, bit_extender_16_out, bit_extender_17_out, bit_extender_18_out,
       bit_extender_19_out, bit_extender_20_out, bit_extender_21_out, bit_extender_22_out,
       bit_extender_23_out, bit_extender_24_out, bit_extender_25_out, bit_extender_26_out,
       bit_extender_27_out, bit_extender_28_out, jalr_rd, jalr_rs1, lbu_rd, lbu_rs1, lui_rd, lw_rd, lw_rs1,
       raddr1, raddr2, sb_rs1, sb_rs2, sw_rs1, sw_rs2, waddr;
  wire [6:0] rom_sum_1_out_2, rom_sum_1_out_2_4;
  wire [24:7] rom_sum_1_out_2_2;
  wire [31:0] add_rddata, add_rs1data, add_rs2data, adder_1_out, addi_rddata, addi_rs1data, and_5_out,
       and_6_out, and_7_out, and_8_out, and_9_out, and_10_out, and_18_out, and_19_out, and_20_out,
       and_21_out, and_22_out, and_23_out, bit_extender_1_out, bit_extender_2_out, bit_extender_3_out,
       bit_extender_4_out, bit_extender_5_out, bit_extender_6_out, bit_extender_7_out, bit_extender_8_out,
       bit_extender_9_out, bit_extender_10_out, bit_extender_11_out, bit_extender_12_out, jalr_newpc,
       jalr_rddata, jalr_rs1data, lbu_ram_addr, lbu_ram_data, lbu_rddata, lbu_rs1data, lui_rddata,
       lw_ram_addr, lw_ram_data, lw_rddata, lw_rs1data, multiplexer_1_out, PC, ram_A, ram_RD, ram_WD, rdata1,
       rdata2, sb_ram_addr, sb_ram_data, sb_rs1data, sb_rs2data, sw_ram_addr, sw_ram_data, sw_rs1data,
       sw_rs2data, undriven, wdata;

  Demultiplexer #(.select(2)) demultiplexer_1 (
    .out0(demultiplexer_1_out0), .out1(demultiplexer_1_out1), .out2(demultiplexer_1_out2),
    .out3(demultiplexer_1_out3), .in(1'b1), .sel(sb_ram_byte));
  assign bit_extender_1_out = {{31{swop}}, swop};  // Bit_Extender bit_extender_1
  assign bit_extender_2_out = {{31{sbop}}, sbop};  // Bit_Extender bit_extender_2
  and and_1 (and_1_out, sbop, demultiplexer_1_out0);
  and and_2 (and_2_out, sbop, demultiplexer_1_out1);
  and and_3 (and_3_out, sbop, demultiplexer_1_out2);
  and and_4 (and_4_out, sbop, demultiplexer_1_out3);
  assign and_5_out = bit_extender_1_out & sw_ram_data;  // AND_Gate and_5, 32 bits wide
  assign and_6_out = bit_extender_2_out & sb_ram_data;  // AND_Gate and_6, 32 bits wide
  Clock clock_1 (.out(clk));
  or or_1 (ram_WE, swop, sbop);
  or or_2 (ram_BE0, swop, and_1_out);
  or or_3 (ram_BE1, swop, and_2_out);
  or or_4 (ram_BE2, swop, and_3_out);
  or or_5 (ram_BE3, swop, and_4_out);
  assign ram_WD = and_5_out | and_6_out;  // OR_Gate or_6, 32 bits wide
  Register #(.width(32)) u_PC (.D(multiplexer_1_out), .en(in_1), .clk(clk), .Q(PC));  // open: clr
  RAM #(.addrWidth(24), .asyncread("true"), .byteenables("byteEnables"), .dataWidth(32), .\type ("nonvolatile")) ram_1 (
    .addr(ram_A[23:0]), .we(ram_WE), .oe(ram_OE), .clk(clk), .din(ram_WD), .dout(ram_RD), .be3(ram_BE3),
    .be2(ram_BE2), .be1(ram_BE1), .be0(ram_BE0));
  Adder #(.width(32)) adder_1 (.a(32'h4), .b(PC), .out(adder_1_out));  // open: cin, cout
  Multiplexer #(.width(32)) multiplexer_1 (.in0(adder_1_out), .in1(jalr_newpc), .out(multiplexer_1_out), .sel(jalrop));
  assign bit_extender_3_out = {{31{lwop}}, lwop};  // Bit_Extender bit_extender_3
  assign and_7_out = bit_extender_3_out & lw_ram_addr;  // AND_Gate and_7, 32 bits wide
  assign bit_extender_4_out = {{31{swop}}, swop};  // Bit_Extender bit_extender_4
  assign and_8_out = bit_extender_4_out & sw_ram_addr;  // AND_Gate and_8, 32 bits wide
  assign bit_extender_5_out = {{31{lbuop}}, lbuop};  // Bit_Extender bit_extender_5
  assign and_9_out = bit_extender_5_out & lbu_ram_addr;  // AND_Gate and_9, 32 bits wide
  assign bit_extender_6_out = {{31{sbop}}, sbop};  // Bit_Extender bit_extender_6
  assign and_10_out = bit_extender_6_out & sb_ram_addr;  // AND_Gate and_10, 32 bits wide
  or or_7 (ram_OE, lwop, lbuop);
  ROM_sum rom_sum_1 (
    .in_1(PC),
    .out_2({rom_sum_1_out_2_4, rom_sum_1_out_2_2[24:15], rom_sum_1_out_2_3, rom_sum_1_out_2_2[11:7], rom_sum_1_out_2}));
  ROM_t1 rom_t1_1 ();  // open: in_1, out_2
  ROM_t2 rom_t2_1 (.in_1(undriven));  // open: out_2
  ROM_t3 rom_t3_1 ();  // open: in_1, out_2
  ROM_t4 rom_t4_1 ();  // open: in_1, out_2
  ROM_t5 rom_t5_1 ();  // open: in_1, out_2
  // Probe on {rom_sum_1_out_2_4, rom_sum_1_out_2_2[24:15], rom_sum_1_out_2_3, rom_sum_1_out_2_2[11:7], rom_sum_1_out_2}
  // ROM_mem rom_mem_1: pin names not known; wires that end beside it: PC, {rom_sum_1_out_2_4, rom_sum_1_out_2_2[24:15], rom_sum_1_out_2_3, rom_sum_1_out_2_2[11:7], rom_sum_1_out_2}
  assign ram_A = and_7_out | and_8_out | and_9_out | and_10_out;  // OR_Gate or_8, 32 bits wide
  Demultiplexer #(.select(3), .width(32)) demultiplexer_2 (
    .out0(lw_ram_data), .out1(lbu_ram_data), .in(ram_RD), .sel(priority_encoder_1_out));  // open: out2, out3, out4, out5, out6, out7
  Priority_Encoder priority_encoder_1 (
    .in0(lwop), .in1(lbuop), .in2(1'b0), .in3(1'b0), .in4(1'b0), .in5(1'b0), .in6(1'b0), .in7(1'b0),
    .out(priority_encoder_1_out));  // open: en_in, gs, en_out
  Comparator #(.width(3)) comparator_1 (.a(rom_sum_1_out_2_3), .b(3'b000), .eq(comparator_1_eq));  // open: gt, lt
  Comparator #(.width(7)) comparator_2 (.a(rom_sum_1_out_2), .b(7'b0100011), .eq(comparator_2_eq));  // open: gt, lt
  Comparator #(.width(3)) comparator_3 (.a(rom_sum_1_out_2_3), .b(3'b100), .eq(comparator_3_eq));  // open: gt, lt
  Comparator #(.width(7)) comparator_4 (.a(rom_sum_1_out_2), .b(7'b0000011), .eq(comparator_4_eq));  // open: gt, lt
  Comparator #(.width(3)) comparator_5 (.a(rom_sum_1_out_2_3), .b(3'b010), .eq(comparator_5_eq));  // open: gt, lt
  Comparator #(.width(7)) comparator_6 (.a(rom_sum_1_out_2), .b(7'b0100011), .eq(comparator_6_eq));  // open: gt, lt
  Comparator #(.width(3)) comparator_7 (.a(rom_sum_1_out_2_3), .b(3'b010), .eq(comparator_7_eq));  // open: gt, lt
  Comparator #(.width(7)) comparator_8 (.a(rom_sum_1_out_2), .b(7'b0000011), .eq(comparator_8_eq));  // open: gt, lt
  Comparator #(.width(7)) comparator_9 (.a(rom_sum_1_out_2), .b(7'b0110111), .eq(luiop));  // open: gt, lt
  Comparator #(.width(3)) comparator_10 (.a(rom_sum_1_out_2_3), .b(3'b000), .eq(comparator_10_eq));  // open: gt, lt
  Comparator #(.width(7)) comparator_11 (.a(rom_sum_1_out_2), .b(7'b1100111), .eq(comparator_11_eq));  // open: gt, lt
  Comparator #(.width(7)) comparator_12 (.a(rom_sum_1_out_2), .b(7'b0010011), .eq(comparator_12_eq));  // open: gt, lt
  Comparator #(.width(3)) comparator_13 (.a(3'b000), .b(rom_sum_1_out_2_3), .eq(comparator_13_eq));  // open: gt, lt
  Comparator #(.width(7)) comparator_14 (.a(rom_sum_1_out_2), .b(7'b0110011), .eq(comparator_14_eq));  // open: gt, lt
  Comparator #(.width(7)) comparator_15 (.a({7{1'b0}}), .b(rom_sum_1_out_2_4), .eq(comparator_15_eq));  // open: gt, lt
  Comparator #(.width(3)) comparator_16 (.a(3'b000), .b(rom_sum_1_out_2_3), .eq(comparator_16_eq));  // open: gt, lt
  and and_11 (sbop, comparator_1_eq, comparator_2_eq);
  and and_12 (lbuop, comparator_3_eq, comparator_4_eq);
  and and_13 (swop, comparator_5_eq, comparator_6_eq);
  and and_14 (lwop, comparator_7_eq, comparator_8_eq);
  and and_15 (jalrop, comparator_10_eq, comparator_11_eq);
  and and_16 (addiop, comparator_12_eq, comparator_13_eq);
  and and_17 (addop, comparator_14_eq, comparator_15_eq, comparator_16_eq);
  or or_9 (wen, lbuop, jalrop, luiop, addop, addiop, lwop);
  assign and_18_out = lbu_rddata & bit_extender_7_out;  // AND_Gate and_18, 32 bits wide
  assign bit_extender_7_out = {{31{lbuop}}, lbuop};  // Bit_Extender bit_extender_7
  assign bit_extender_8_out = {{31{jalrop}}, jalrop};  // Bit_Extender bit_extender_8
  assign and_19_out = bit_extender_8_out & jalr_rddata;  // AND_Gate and_19, 32 bits wide
  assign bit_extender_9_out = {{31{addop}}, addop};  // Bit_Extender bit_extender_9
  assign and_20_out = lui_rddata & bit_extender_10_out;  // AND_Gate and_20, 32 bits wide
  assign bit_extender_10_out = {{31{luiop}}, luiop};  // Bit_Extender bit_extender_10
  assign and_21_out = addi_rddata & bit_extender_11_out;  // AND_Gate and_21, 32 bits wide
  assign bit_extender_11_out = {{31{addiop}}, addiop};  // Bit_Extender bit_extender_11
  assign and_22_out = lw_rddata & bit_extender_12_out;  // AND_Gate and_22, 32 bits wide
  assign bit_extender_12_out = {{31{lwop}}, lwop};  // Bit_Extender bit_extender_12
  assign bit_extender_13_out = {{4{lbuop}}, lbuop};  // Bit_Extender bit_extender_13
  assign bit_extender_14_out = {{4{jalrop}}, jalrop};  // Bit_Extender bit_extender_14
  assign bit_extender_15_out = {{4{luiop}}, luiop};  // Bit_Extender bit_extender_15
  assign bit_extender_16_out = {{4{addiop}}, addiop};  // Bit_Extender bit_extender_16
  assign bit_extender_17_out = {{4{lwop}}, lwop};  // Bit_Extender bit_extender_17
  assign and_23_out = add_rddata & bit_extender_9_out;  // AND_Gate and_23, 32 bits wide
  assign and_24_out = lbu_rd & bit_extender_13_out;  // AND_Gate and_24, 5 bits wide
  assign and_25_out = bit_extender_14_out & jalr_rd;  // AND_Gate and_25, 5 bits wide
  assign and_26_out = add_rd & bit_extender_18_out;  // AND_Gate and_26, 5 bits wide
  assign bit_extender_18_out = {{4{addop}}, addop};  // Bit_Extender bit_extender_18
  assign and_27_out = lui_rd & bit_extender_15_out;  // AND_Gate and_27, 5 bits wide
  assign and_28_out = addi_rd & bit_extender_16_out;  // AND_Gate and_28, 5 bits wide
  assign and_29_out = lw_rd & bit_extender_17_out;  // AND_Gate and_29, 5 bits wide
  assign wdata = and_18_out | and_19_out | and_23_out | and_20_out | and_21_out | and_22_out;  // OR_Gate or_10, 32 bits wide
  assign waddr = and_24_out | and_25_out | and_26_out | and_27_out | and_28_out | and_29_out;  // OR_Gate or_11, 5 bits wide
  my_sb my_sb_1 (
    .I({rom_sum_1_out_2_4, rom_sum_1_out_2_2[24:15], rom_sum_1_out_2_3, rom_sum_1_out_2_2[11:7], rom_sum_1_out_2}),
    .rs1data(sb_rs1data), .rs2data(sb_rs2data), .rs1(sb_rs1), .ram_byte(sb_ram_byte), .rs2(sb_rs2),
    .ram_addr(sb_ram_addr), .ram_data(sb_ram_data));
  my_sw my_sw_1 (
    .I({rom_sum_1_out_2_4, rom_sum_1_out_2_2[24:15], rom_sum_1_out_2_3, rom_sum_1_out_2_2[11:7], rom_sum_1_out_2}),
    .rs1data(sw_rs1data), .rs2data(sw_rs2data), .rs1(sw_rs1), .rs2(sw_rs2), .ram_addr(sw_ram_addr),
    .ram_data(sw_ram_data));
  my_lw my_lw_1 (
    .I({rom_sum_1_out_2_4, rom_sum_1_out_2_2[24:15], rom_sum_1_out_2_3, rom_sum_1_out_2_2[11:7], rom_sum_1_out_2}),
    .rs1data(lw_rs1data), .ram_data(lw_ram_data), .rd(lw_rd), .rs1(lw_rs1), .ram_addr(lw_ram_addr),
    .rddata(lw_rddata));
  my_lui my_lui_1 (
    .I({rom_sum_1_out_2_4, rom_sum_1_out_2_2[24:15], rom_sum_1_out_2_3, rom_sum_1_out_2_2[11:7], rom_sum_1_out_2}),
    .rd(lui_rd), .rddata(lui_rddata));
  my_add my_add_1 (
    .I({rom_sum_1_out_2_4, rom_sum_1_out_2_2[24:15], rom_sum_1_out_2_3, rom_sum_1_out_2_2[11:7], rom_sum_1_out_2}),
    .rs2data(add_rs2data), .rs1data(add_rs1data), .rd(add_rd), .rs1(add_rs1), .rs2(add_rs2),
    .rddata(add_rddata));
  my_jalr my_jalr_1 (
    .I({rom_sum_1_out_2_4, rom_sum_1_out_2_2[24:15], rom_sum_1_out_2_3, rom_sum_1_out_2_2[11:7], rom_sum_1_out_2}),
    .rs1data(jalr_rs1data), .PC(PC), .rd(jalr_rd), .rs1(jalr_rs1), .newpc(jalr_newpc), .rddata(jalr_rddata));
  my_addi my_addi_1 (
    .I({rom_sum_1_out_2_4, rom_sum_1_out_2_2[24:15], rom_sum_1_out_2_3, rom_sum_1_out_2_2[11:7], rom_sum_1_out_2}),
    .rs1data(addi_rs1data), .rd(addi_rd), .rs1(addi_rs1), .rddata(addi_rddata));
  my_lbu my_lbu_1 (
    .ram_data(lbu_ram_data),
    .I({rom_sum_1_out_2_4, rom_sum_1_out_2_2[24:15], rom_sum_1_out_2_3, rom_sum_1_out_2_2[11:7], rom_sum_1_out_2}),
    .rs1data(lbu_rs1data), .rddata(lbu_rddata), .rd(lbu_rd), .rs1(lbu_rs1), .ram_addr(lbu_ram_addr));
  assign bit_extender_19_out = {{4{swop}}, swop};  // Bit_Extender bit_extender_19
  assign bit_extender_20_out = {{4{lbuop}}, lbuop};  // Bit_Extender bit_extender_20
  assign bit_extender_21_out = {{4{lwop}}, lwop};  // Bit_Extender bit_extender_21
  assign bit_extender_22_out = {{4{sbop}}, sbop};  // Bit_Extender bit_extender_22
  assign and_30_out = sw_rs1 & bit_extender_19_out;  // AND_Gate and_30, 5 bits wide
  assign bit_extender_23_out = {{4{jalrop}}, jalrop};  // Bit_Extender bit_extender_23
  assign and_31_out = bit_extender_23_out & jalr_rs1;  // AND_Gate and_31, 5 bits wide
  assign and_32_out = add_rs1 & bit_extender_24_out;  // AND_Gate and_32, 5 bits wide
  assign bit_extender_24_out = {{4{addop}}, addop};  // Bit_Extender bit_extender_24
  assign and_33_out = lbu_rs1 & bit_extender_20_out;  // AND_Gate and_33, 5 bits wide
  assign and_34_out = lw_rs1 & bit_extender_21_out;  // AND_Gate and_34, 5 bits wide
  assign and_35_out = addi_rs1 & bit_extender_25_out;  // AND_Gate and_35, 5 bits wide
  assign bit_extender_25_out = {{4{addiop}}, addiop};  // Bit_Extender bit_extender_25
  assign and_36_out = sb_rs1 & bit_extender_22_out;  // AND_Gate and_36, 5 bits wide
  Demultiplexer #(.select(3), .width(32)) demultiplexer_3 (
    .out0(addi_rs1data), .out1(jalr_rs1data), .out2(add_rs1data), .out3(lw_rs1data), .out4(sw_rs1data),
    .out5(lbu_rs1data), .out6(sb_rs1data), .in(rdata1), .sel(priority_encoder_2_out));  // open: out7
  Priority_Encoder priority_encoder_2 (
    .in0(addiop), .in1(jalrop), .in2(addop), .in3(lwop), .in4(swop), .in5(lbuop), .in6(sbop), .in7(1'b0),
    .out(priority_encoder_2_out));  // open: en_in, gs, en_out
  assign raddr1 = and_30_out | and_31_out | and_32_out | and_33_out | and_34_out | and_35_out | and_36_out;  // OR_Gate or_12, 5 bits wide
  GPR gpr_1 (
    .clk(clk), .wdata(wdata), .waddr(waddr), .wen(wen), .raddr1(raddr1), .raddr2(raddr2), .rdata1(rdata1),
    .rdata2(rdata2));
  assign and_37_out = add_rs2 & bit_extender_26_out;  // AND_Gate and_37, 5 bits wide
  assign bit_extender_26_out = {{4{addop}}, addop};  // Bit_Extender bit_extender_26
  assign and_38_out = sb_rs2 & bit_extender_27_out;  // AND_Gate and_38, 5 bits wide
  assign bit_extender_27_out = {{4{sbop}}, sbop};  // Bit_Extender bit_extender_27
  assign and_39_out = sw_rs2 & bit_extender_28_out;  // AND_Gate and_39, 5 bits wide
  assign bit_extender_28_out = {{4{swop}}, swop};  // Bit_Extender bit_extender_28
  assign raddr2 = and_37_out | and_38_out | and_39_out;  // OR_Gate or_13, 5 bits wide
  Demultiplexer #(.select(3), .width(32)) demultiplexer_4 (
    .out0(add_rs2data), .out1(sw_rs2data), .out2(sb_rs2data), .in(rdata2), .sel(priority_encoder_3_out));  // open: out3, out4, out5, out6, out7
  Priority_Encoder priority_encoder_3 (
    .in0(addop), .in1(swop), .in2(sbop), .in3(1'b0), .in4(1'b0), .in5(1'b0), .in6(1'b0), .in7(1'b0),
    .out(priority_encoder_3_out));  // open: en_in, gs, en_out

  // Notes on the sheet:
  //   RAM写
  //   RAM读
  //   opcode
  //   funct3
  //   funct7
  //   sb
  //   lbu
  //   sw
  //   lw
  //   lui
  //   jalr
  //   addi
  //   add
  //   写端口
  //   读1
  //   读2
endmodule

module GPR (
  input  clk,
  input  [31:0] wdata,
  input  [4:0] waddr,
  input  wen,
  input  [4:0] raddr1,
  input  [4:0] raddr2,
  output [31:0] rdata1,
  output [31:0] rdata2
);

  wire decoder_1_out1, decoder_1_out2, decoder_1_out3, decoder_1_out4, decoder_1_out5, decoder_1_out6,
       decoder_1_out7, decoder_1_out8, decoder_1_out9, decoder_1_out10, decoder_1_out11, decoder_1_out12,
       decoder_1_out13, decoder_1_out14, decoder_1_out15;
  wire [31:0] register_1_q, register_2_q, register_3_q, register_4_q, register_5_q, register_6_q,
       register_7_q, register_8_q, register_9_q, register_10_q, register_11_q, register_12_q, register_13_q,
       register_14_q, register_15_q, register_16_q;

  Decoder #(.select(4)) decoder_1 (
    .out1(decoder_1_out1), .out2(decoder_1_out2), .out3(decoder_1_out3), .out4(decoder_1_out4),
    .out5(decoder_1_out5), .out6(decoder_1_out6), .out7(decoder_1_out7), .out8(decoder_1_out8),
    .out9(decoder_1_out9), .out10(decoder_1_out10), .out11(decoder_1_out11), .out12(decoder_1_out12),
    .out13(decoder_1_out13), .out14(decoder_1_out14), .out15(decoder_1_out15), .sel(waddr[3:0]), .en(wen));  // open: out0
  Register #(.width(32)) register_1 (.D(wdata), .en(decoder_1_out1), .clk(clk), .Q(register_1_q), .clr(1'b1));
  Register #(.width(32)) register_2 (.D(wdata), .en(decoder_1_out8), .clk(clk), .Q(register_2_q));  // open: clr
  Register #(.width(32)) register_3 (.D(wdata), .en(decoder_1_out1), .clk(clk), .Q(register_3_q));  // open: clr
  Register #(.width(32)) register_4 (.D(wdata), .en(decoder_1_out9), .clk(clk), .Q(register_4_q));  // open: clr
  Register #(.width(32)) register_5 (.D(wdata), .en(decoder_1_out2), .clk(clk), .Q(register_5_q));  // open: clr
  Register #(.width(32)) register_6 (.D(wdata), .en(decoder_1_out10), .clk(clk), .Q(register_6_q));  // open: clr
  Register #(.width(32)) register_7 (.D(wdata), .en(decoder_1_out3), .clk(clk), .Q(register_7_q));  // open: clr
  Register #(.width(32)) register_8 (.D(wdata), .en(decoder_1_out11), .clk(clk), .Q(register_8_q));  // open: clr
  Register #(.width(32)) register_9 (.D(wdata), .en(decoder_1_out4), .clk(clk), .Q(register_9_q));  // open: clr
  Register #(.width(32)) register_10 (.D(wdata), .en(decoder_1_out12), .clk(clk), .Q(register_10_q));  // open: clr
  Register #(.width(32)) register_11 (.D(wdata), .en(decoder_1_out5), .clk(clk), .Q(register_11_q));  // open: clr
  Register #(.width(32)) register_12 (.D(wdata), .en(decoder_1_out13), .clk(clk), .Q(register_12_q));  // open: clr
  Register #(.width(32)) register_13 (.D(wdata), .en(decoder_1_out6), .clk(clk), .Q(register_13_q));  // open: clr
  Register #(.width(32)) register_14 (.D(wdata), .en(decoder_1_out14), .clk(clk), .Q(register_14_q));  // open: clr
  Register #(.width(32)) register_15 (.D(wdata), .en(decoder_1_out7), .clk(clk), .Q(register_15_q));  // open: clr
  Register #(.width(32)) register_16 (.D(wdata), .en(decoder_1_out15), .clk(clk), .Q(register_16_q));  // open: clr
  Multiplexer #(.select(4), .width(32)) multiplexer_1 (
    .in0(register_1_q), .in1(register_3_q), .in2(register_5_q), .in3(register_7_q), .in4(register_9_q),
    .in5(register_11_q), .in6(register_13_q), .in7(register_15_q), .in8(register_2_q), .in9(register_4_q),
    .in10(register_6_q), .in11(register_8_q), .in12(register_10_q), .in13(register_12_q),
    .in14(register_14_q), .in15(register_16_q), .out(rdata1), .sel(raddr1[3:0]));
  Multiplexer #(.select(4), .width(32)) multiplexer_2 (
    .in0(register_1_q), .in1(register_3_q), .in2(register_5_q), .in3(register_7_q), .in4(register_9_q),
    .in5(register_11_q), .in6(register_13_q), .in7(register_15_q), .in8(register_2_q), .in9(register_4_q),
    .in10(register_6_q), .in11(register_8_q), .in12(register_10_q), .in13(register_12_q),
    .in14(register_14_q), .in15(register_16_q), .out(rdata2), .sel(raddr2[3:0]));
endmodule

module ROM_t1 (
  input  [31:0] in_1,
  output [31:0] out_2
);

  ROM #(.dataWidth(32)) rom_1 (.addr(in_1[9:2]), .data(out_2));

  // Notes on the sheet:
  //   contents of rom_1 (hex, n*v repeats v):
  //   ffe00513 10000e7 c000e7 c00067 a50513 8067
endmodule

module my_addi (
  input  [31:0] I,
  input  [31:0] rs1data,
  output [4:0] rd,
  output [4:0] rs1,
  output [31:0] rddata
);

  wire [31:0] bit_extender_1_out;

  assign bit_extender_1_out = {{20{I[31]}}, I[31:20]};  // Bit_Extender bit_extender_1
  Adder #(.width(32)) adder_1 (.a(bit_extender_1_out), .b(rs1data), .out(rddata));  // open: cin, cout

  assign rd = I[11:7];
  assign rs1 = I[19:15];
endmodule

module my_jalr (
  input  [31:0] I,
  input  [31:0] rs1data,
  input  [31:0] PC,
  output [4:0] rd,
  output [4:0] rs1,
  output [31:0] newpc,
  output [31:0] rddata
);

  wire [31:0] bit_extender_1_out;

  assign bit_extender_1_out = {{20{I[31]}}, I[31:20]};  // Bit_Extender bit_extender_1
  Adder #(.width(32)) adder_1 (.a(PC), .b(32'h4), .out(rddata));  // open: cin, cout
  Adder #(.width(32)) adder_2 (.a(bit_extender_1_out), .b(rs1data), .out(newpc));  // open: cin, cout

  assign rd = I[11:7];
  assign rs1 = I[19:15];

  // Notes on the sheet:
  //   把当前的下一条指令地址存入rd
endmodule

module my_add (
  input  [31:0] I,
  input  [31:0] rs2data,
  input  [31:0] rs1data,
  output [4:0] rd,
  output [4:0] rs1,
  output [4:0] rs2,
  output [31:0] rddata
);

  Adder #(.width(32)) adder_1 (.a(rs2data), .b(rs1data), .out(rddata));  // open: cin, cout

  assign rd = I[11:7];
  assign rs1 = I[19:15];
  assign rs2 = I[24:20];
endmodule

module my_lui (
  input  [31:0] I,
  output [4:0] rd,
  output [31:0] rddata
);


  assign rd = I[11:7];
  assign rddata = {I[31:12], {12{1'b0}}};
endmodule

module ROM_t2 (
  input  [31:0] in_1,
  output [31:0] out_2
);

  ROM #(.dataWidth(32)) rom_1 (.addr(in_1[9:2]), .data(out_2));

  // Notes on the sheet:
  //   contents of rom_1 (hex, n*v repeats v):
  //   123450b7 67808093 1000113 2081b3 10067
endmodule

module my_lw (
  input  [31:0] I,
  input  [31:0] rs1data,
  input  [31:0] ram_data,
  output [4:0] rd,
  output [4:0] rs1,
  output [31:0] ram_addr,
  output [31:0] rddata
);

  wire [1:0] adder_1_out;
  wire [31:0] bit_extender_1_out;

  assign bit_extender_1_out = {{20{I[31]}}, I[31:20]};  // Bit_Extender bit_extender_1
  Adder #(.width(32)) adder_1 (
    .a(bit_extender_1_out), .b(rs1data), .out({ram_addr[29:0], adder_1_out}));  // open: cin, cout

  assign ram_addr[31:30] = 2'b00;
  assign rd = I[11:7];
  assign rddata = ram_data;
  assign rs1 = I[19:15];
endmodule

module my_sw (
  input  [31:0] I,
  input  [31:0] rs1data,
  input  [31:0] rs2data,
  output [4:0] rs1,
  output [4:0] rs2,
  output [31:0] ram_addr,
  output [31:0] ram_data
);

  wire [1:0] adder_1_out;
  wire [31:0] bit_extender_1_out;

  assign bit_extender_1_out = {{20{I[31]}}, {I[31:25], I[11:7]}};  // Bit_Extender bit_extender_1
  Adder #(.width(32)) adder_1 (
    .a(bit_extender_1_out), .b(rs1data), .out({ram_addr[29:0], adder_1_out}));  // open: cin, cout

  assign ram_addr[31:30] = 2'b00;
  assign ram_data = rs2data;
  assign rs1 = I[19:15];
  assign rs2 = I[24:20];
endmodule

module ROM_t3 (
  input  [31:0] in_1,
  output [31:0] out_2
);

  ROM #(.dataWidth(32)) rom_1 (.addr(in_1[9:2]), .data(out_2));

  // Notes on the sheet:
  //   contents of rom_1 (hex, n*v repeats v):
  //   40a103 20a023
endmodule

module my_lbu (
  input  [31:0] ram_data,
  input  [31:0] I,
  input  [31:0] rs1data,
  output [31:0] rddata,
  output [4:0] rd,
  output [4:0] rs1,
  output [31:0] ram_addr
);

  wire [1:0] adder_1_out;
  wire [31:0] bit_extender_1_out;

  assign bit_extender_1_out = {{20{I[31]}}, I[31:20]};  // Bit_Extender bit_extender_1
  Adder #(.width(32)) adder_1 (
    .a(bit_extender_1_out), .b(rs1data), .out({ram_addr[29:0], adder_1_out}));  // open: cin, cout
  Multiplexer #(.select(2), .width(8)) multiplexer_1 (
    .in0(ram_data[7:0]), .in1(ram_data[15:8]), .in2(ram_data[23:16]), .in3(ram_data[31:24]),
    .out(rddata[7:0]), .sel(adder_1_out));

  assign ram_addr[31:30] = 2'b00;
  assign rd = I[11:7];
  assign rddata[31:8] = {24{1'b0}};
  assign rs1 = I[19:15];
endmodule

module ROM_t4 (
  input  [31:0] in_1,
  output [31:0] out_2
);

  ROM #(.dataWidth(32)) rom_1 (.addr(in_1[9:2]), .data(out_2));

  // Notes on the sheet:
  //   contents of rom_1 (hex, n*v repeats v):
  //   4083 104103 204183 304203
endmodule

module my_sb (
  input  [31:0] I,
  input  [31:0] rs1data,
  input  [31:0] rs2data,
  output [4:0] rs1,
  output [1:0] ram_byte,
  output [4:0] rs2,
  output [31:0] ram_addr,
  output [31:0] ram_data
);

  wire [31:0] bit_extender_1_out;

  assign bit_extender_1_out = {{20{I[31]}}, {I[31:25], I[11:7]}};  // Bit_Extender bit_extender_1
  Demultiplexer #(.select(2), .width(8)) demultiplexer_1 (
    .out0(ram_data[7:0]), .out1(ram_data[15:8]), .out2(ram_data[23:16]), .out3(ram_data[31:24]),
    .in(rs2data[7:0]), .sel(ram_byte));
  Adder #(.width(32)) adder_1 (
    .a(bit_extender_1_out), .b(rs1data), .out({ram_addr[29:0], ram_byte}));  // open: cin, cout

  assign ram_addr[31:30] = 2'b00;
  assign rs1 = I[19:15];
  assign rs2 = I[24:20];
endmodule

module ROM_t5 (
  input  [31:0] in_1,
  output [31:0] out_2
);

  ROM #(.dataWidth(32)) rom_1 (.addr(in_1[9:2]), .data(out_2));

  // Notes on the sheet:
  //   contents of rom_1 (hex, n*v repeats v):
  //   2083 9000113 ab00193 cd00213 ef00293 2001a3 300123 4000a3 500023 2303
endmodule

module ROM_mem (
  input  [31:0] in_1,
  output [31:0] out_2
);

  ROM #(.addrWidth(24), .dataWidth(32)) rom_1 (.addr(in_1[25:2]), .data(out_2));

  // Notes on the sheet:
  //   contents of rom_1 (hex, n*v repeats v):
  //   413 52137 10113 10b7 22408093 80e7 fea12823 fe812e23 1437 40840413 ff014183 3401b3 1c183 ff114203
  //   440233 24203 4181b3 ff214203 440233 24203 4181b3 ff314203 440233 24203 4181b3 1237 40020213 320233
  //   24203 ffc12403 420233 420233 410233 a000193 fe312823 9c00193 fe312623 fec22203 20067 8067 ff410113
  //   100513 112423 10b7 21808093 80e7 fec10113 912423 494b7 6b048493 812623 112823 496b7 69068693 48413
  //   48713 fe012823 174183 fe3109a3 ff012183 fe812e23 fe312823 3d437 60040413 ff214203 420233 420233
  //   440233 22203 fe412623 ff114203 420233 420233 440233 22203 fe412423 ff014203 420233 420233 440233
  //   22203 fe412223 fed14183 fea14203 4181b3 fe714203 4181b3 fe312223 fee14183 feb14203 4181b3 fe3102a3
  //   fef14183 fe310323 fe412183 8237 20213 440433 ff314203 420233 420233 440233 22203 ffc12403 4181b3
  //   74503 350533 6a603 270713 468693 fe312a23 fec12423 31237 50020213 feb14183 4181b3 1c183 fe3103a3
  //   fea14183 4181b3 1c183 fe310323 fe914183 4181b3 1c183 fe3102a3 fe814183 4181b3 1c183 fe310223
  //   ff412183 fe412203 450533 150513 fea12823 fe812e23 1437 40840413 ff014183 3401b3 1c183 ff114203
  //   440233 24203 4181b3 ff214203 440233 24203 4181b3 ff314203 440233 24203 4181b3 1237 40020213 320233
  //   24503 ffc12403 e12223 d12023 1800093 80e7 412703 497b7 6c078793 12683 fee12823 fef12623 fe812e23
  //   fe912c23 1437 30040413 ff014183 340233 100193 320023 fec14183 3401b3 18023 24183 ff114483 940233
  //   100493 920023 fed14483 9404b3 48023 24483 9181b3 ff214483 940233 100493 920023 fee14483 9404b3 48023
  //   24483 9181b3 ff314483 940233 100493 920023 fef14483 9404b3 48023 24483 9181b3 1237 40020213 320233
  //   24203 ff812483 ffc12403 420233 420233 410233 37800193 fe312823 e000193 fe312623 fec22203 20067 49737
  //   67070713 72683 fe012823 14c203 fe4108a3 ff012203 4c503 450533 470713 e12023 fe312a23 fed12423 31237
  //   50020213 feb14183 4181b3 1c183 fe3103a3 fea14183 4181b3 1c183 fe310323 fe914183 4181b3 1c183
  //   fe3102a3 fe814183 4181b3 1c183 fe310223 ff412183 fe412203 450533 150513 fea12823 fe812e23 1437
  //   40840413 ff014183 3401b3 1c183 ff114203 440233 24203 4181b3 ff214203 440233 24203 4181b3 ff314203
  //   440233 24203 4181b3 1237 40020213 320233 24503 ffc12403 1800093 80e7 248493 497b7 6c078793 12703
  //   fe912823 fef12623 fe812e23 fe912c23 1437 30040413 ff014183 340233 100193 320023 fec14183 3401b3
  //   18023 24183 ff114483 940233 100493 920023 fed14483 9404b3 48023 24483 9181b3 ff214483 940233 100493
  //   920023 fee14483 9404b3 48023 24483 9181b3 ff314483 940233 100493 920023 fef14483 9404b3 48023 24483
  //   9181b3 1237 40020213 320233 24203 ff812483 ffc12403 420233 420233 410233 55c00193 fe312823 38000193
  //   fe312623 fec22203 20067 244683 144603 344703 444783 494b7 64048493 8*d686b3 fed12823 fec12623 116b7
  //   60068693 fe012223 ff314203 fe4102a3 fef14203 fe410223 fe412203 468233 24203 fe4105a3 ff214203
  //   fe4102a3 fee14203 fe410223 fe412203 468233 24203 fe410523 ff114203 fe4102a3 fed14203 fe410223
  //   fe412203 468233 24203 fe4104a3 ff014203 fe4102a3 fec14203 fe410223 fe412203 468233 24203 fe410423
  //   fe812683 4a503 fe012823 fee10923 fee12423 fe914203 fe4109a3 ff012703 fee12823 fed12623 11737
  //   60070713 fe012223 ff314203 fe4102a3 fef14203 fe410223 fe412203 470233 24203 fe4105a3 ff214203
  //   fe4102a3 fee14203 fe410223 fe412203 470233 24203 fe410523 ff114203 fe4102a3 fed14203 fe410223
  //   fe412203 470233 24203 fe4104a3 ff014203 fe4102a3 fec14203 fe410223 fe412203 470233 24203 fe410423
  //   fe812703 fe012823 fef109a3 ff012783 fef12823 fee12623 117b7 60078793 fe012223 ff314203 fe4102a3
  //   fef14203 fe410223 fe412203 478233 24203 fe4105a3 ff214203 fe4102a3 fee14203 fe410223 fe412203 478233
  //   24203 fe410523 ff114203 fe4102a3 fed14203 fe410223 fe412203 478233 24203 fe4104a3 ff014203 fe4102a3
  //   fec14203 fe410223 fe412203 478233 24203 fe410423 fe812783 fe312a23 fef12423 31237 50020213 feb14183
  //   4181b3 1c183 fe3103a3 fea14183 4181b3 1c183 fe310323 fe914183 4181b3 1c183 fe3102a3 fe814183 4181b3
  //   1c183 fe310223 ff412183 fe412203 450533 150513 fea12823 fe812e23 1437 40840413 ff014183 3401b3 1c183
  //   ff114203 440233 24203 4181b3 ff214203 440233 24203 4181b3 ff314203 440233 24203 4181b3 1237 400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
endmodule

module ROM_sum (
  input  [31:0] in_1,
  output [31:0] out_2
);

  ROM #(.addrWidth(24), .dataWidth(32)) rom_1 (.addr(in_1[25:2]), .data(out_2));

  // Notes on the sheet:
  //   contents of rom_1 (hex, n*v repeats v):
  //   413 51137 10113 22c00093 80e7 fea12823 fe812e23 40800413 ff014183 3401b3 1c183 ff114203 440233 24203
  //   4181b3 ff214203 440233 24203 4181b3 ff314203 440233 24203 4181b3 40000213 320233 24203 ffc12403
  //   420233 420233 410233 9400193 fe312823 9000193 fe312623 fec22203 20067 8067 ff410113 100513 112423
  //   22400093 80e7 ff010113 112623 12023 100793 6500693 12703 f70733 e12023 178793 fef12823 fed12623
  //   fe812e23 fe912c23 30000413 ff014183 340233 100193 320023 fec14183 3401b3 18023 24183 ff114483 940233
  //   100493 920023 fed14483 9404b3 48023 24483 9181b3 ff214483 940233 100493 920023 fee14483 9404b3 48023
  //   24483 9181b3 ff314483 940233 100493 920023 fef14483 9404b3 48023 24483 9181b3 40000213 320233 24203
  //   ff812483 ffc12403 420233 420233 410233 1a400193 fe312823 bc00193 fe312623 fec22203 20067 12503
  //   fffff7b7 c4678793 f50533 fea12823 fe812e23 40800413 ff014183 3401b3 1c183 ff114203 440233 24203
  //   4181b3 ff214203 440233 24203 4181b3 ff314203 440233 24203 4181b3 40000213 320233 24503 ffc12403
  //   1400093 80e7 c12083 513 1010113 8067 22400213 20067 ff410113 48537 60050513 112423 a800093 80e7
  //   22400093 80e7 109*0 1 0 1010100 63*1010101 100 1000101 1010100 1000000 1010100 121*0 64*1000100
  //   64*2020000 64*3020100 0 4040404 0 4040404 0 4040404 0 4040404 0 4040404 0 4040404 0 4040404 0
  //   4040404 0 4040404 0 4040404 0 4040404 0 4040404 0 4040404 0 4040404 0 4040404 0 4040404 0 4040404 0
  //   4040404 0 4040404 0 4040404 0 4040404 0 4040404 0 4040404 0 4040404 0 4040404 0 4040404 0 4040404 0
  //   4040404 0 4040404 0 4040404 0 4040404 0 4040404 1000100 5040504 1000100 5040504 1000100 5040504
  //   1000100 5040504 1000100 5040504 1000100 5040504 1000100 5040504 1000100 5040504 1000100 5040504
  //   1000100 5040504 1000100 5040504 1000100 5040504 1000100 5040504 1000100 5040504 1000100 5040504
  //   1000100 5040504 1000100 5040504 1000100 5040504 1000100 5040504 1000100 5040504 1000100 5040504
  //   1000100 5040504 1000100 5040504 1000100 5040504 1000100 5040504 1000100 5040504 1000100 5040504
  //   1000100 5040504 1000100 5040504 1000100 5040504 1000100 5040504 1000100 5040504 2020000 6060404
  //   2020000 6060404 2020000 6060404 2020000 6060404 2020000 6060404 2020000 6060404 2020000 6060404
  //   2020000 6060404 2020000 6060404 2020000 6060404 2020000 6060404 2020000 6060404 2020000 6060404
  //   2020000 6060404 2020000 6060404 2020000 6060404 2020000 6060404 2020000 6060404 2020000 6060404
  //   2020000 6060404 2020000 6060404 2020000 6060404 2020000 6060404 2020000 6060404 2020000 6060404
  //   2020000 6060404 2020000 6060404 2020000 6060404 2020000 6060404 2020000 6060404 2020000 6060404
  //   2020000 6060404 3020100 7060504 3020100 7060504 3020100 7060504 3020100 7060504 3020100 7060504
  //   3020100 7060504 3020100 7060504 3020100 7060504 3020100 7060504 3020100 7060504 3020100 7060504
  //   3020100 7060504 3020100 7060504 3020100 7060504 3020100 7060504 3020100 7060504 3020100 7060504
  //   3020100 7060504 3020100 7060504 3020100 7060504 3020100 7060504 3020100 7060504 3020100 7060504
  //   3020100 7060504 3020100 7060504 3020100 7060504 3020100 7060504 3020100 7060504 3020100 7060504
  //   3020100 7060504 3020100 7060504 3020100 7060504 0 0 8080808 8080808 0 0 8080808 8080808 0 0 8080808
  //   8080808 0 0 8080808 8080808 0 0 8080808 8080808 0 0 8080808 8080808 0 0 8080808 8080808 0 0 8080808
  //   8080808 0 0 8080808 8080808 0 0 8080808 8080808 0 0 8080808 8080808 0 0 8080808 8080808 0 0 8080808
  //   8080808 0 0 8080808 8080808 0 0 8080808 8080808 0 0 8080808 8080808 1000100 1000100 9080908 9080908
  //   1000100 1000100 9080908 9080908 1000100 1000100 9080908 9080908 1000100 1000100 9080908 9080908
  //   1000100 1000100 9080908 9080908 1000100 1000100 9080908 9080908 1000100 1000100 9080908 9080908
  //   1000100 1000100 9080908 9080908 1000100 1000100 9080908 9080908 1000100 1000100 9080908 9080908
  //   1000100 1000100 9080908 9080908 1000100 1000100 9080908 9080908 1000100 1000100 9080908 9080908
  //   1000100 1000100 9080908 9080908 1000100 1000100 9080908 9080908 1000100 1000100 9080908 9080908
  //   2020000 2020000 a0a0808 a0a0808 2020000 2020000 a0a0808 a0a0808 2020000 2020000 a0a0808 a0a0808
  //   2020000 2020000 a0a080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
endmodule
